// Digital circuit boolean_operators_with_transistors.dig as structural Verilog
module boolean_operators_with_transistors (
  input  not_a,
  input  or_a,
  input  or_b,
  input  and_a,
  input  and_b,
  output not_o,
  output or_o,
  output and_o
);

  wire nfet_4_s;

  PullUp pullup_1 (.out(not_o));
  NFET nfet_1 (.G(not_a), .D(not_o), .S(1'b0));
  NFET nfet_2 (.G(or_a), .D(1'b1), .S(or_o));
  NFET nfet_3 (.G(or_b), .D(1'b1), .S(or_o));
  PullDown pulldown_1 (.out(or_o));
  NFET nfet_4 (.G(and_a), .D(1'b1), .S(nfet_4_s));
  NFET nfet_5 (.G(and_b), .D(nfet_4_s), .S(and_o));
  PullDown pulldown_2 (.out(and_o));

  // Notes on the sheet:
  //   Not
  //   Or
  //   And
endmodule

/* Test case not_test:
not_a 	not_o
0	1
1	0
*/

/* Test case or_test:
or_a	or_b	or_o
0	0	0
0	1	1
1	0	1
1	1	1
*/

/* Test case and_test:
and_a	and_b	and_o
0	0	0
0	1	0
1	0	0
1	1	0
*/
