// Digital circuit 1_1-counter.dig as structural Verilog
module _1_1_counter (
  input  C,
  input  EN,
  output O_0,
  output O_1,
  output O_2,
  output O_3
);

  Register #(.Bits(4)) register_1 ();  // open: D, C, en, Q
  Add #(.Bits(4)) add_1 (.b(4'b0001), .c_i(1'b0));  // open: a, s, c_o

  // Notes on the sheet:
  //   4 Bit Counter
endmodule

/* Test case 4 bit counter_test:
EN	O_3	O_2	O_1	O_0	C
# Pulse while not enabled
0	0	0	0	0	C
0	0	0	0	0	C
# Pulse while enabled
1	0	0	0	1	C
1	0	0	1	0	C
1	0	0	1	1	C
1	0	1	0	0	C
1	0	1	0	1	C
1	0	1	1	0	C
1	0	1	1	1	C
1	1	0	0	0	C
1	1	0	0	1	C
1	1	0	1	0	C
1	1	0	1	1	C
1	1	1	0	0	C
1	1	1	0	1	C
1	1	1	1	0	C
1	1	1	1	1	C
# Pulse while not enabled
0	1	1	1	1	C
0	1	1	1	1	C
# Overflow
1	0	0	0	0	C
*/
