// Digital circuit 1_2-counter_load.dig as structural Verilog
module _1_2_counter_load (
  input  C,
  input  D_0,
  input  D_1,
  input  D_2,
  input  D_3,
  input  EN,
  input  Out,
  input  In,
  output O_0,
  output O_1,
  output O_2,
  output O_3
);

  Register #(.Bits(4)) register_1 ();  // open: D, C, en, Q
  Add #(.Bits(4)) add_1 (.b(4'b0001), .c_i(1'b0));  // open: a, s, c_o
  // Or or_1 is placed but not wired
  Multiplexer #(.Bits(4)) multiplexer_1 ();  // open: sel, in_0, in_1, out
  Driver #(.Bits(4)) driver_1 ();  // open: in, en, out

  assign O_0 = D_0;
  assign O_1 = D_1;
  assign O_2 = D_2;
  assign O_3 = D_3;

  // Notes on the sheet:
  //   4 Bit Counter Load
endmodule

/* Test case 4 bit counter load_test:
EN	In	Out	D_3	D_2	D_1	D_0	O_3	O_2	O_1	O_0	C
0	0	0	X	X	X	X	X	X	X	X	C
# Pulse with enable no output
1	0	0	Z	Z	Z	Z	Z	Z	Z	Z	C
1	0	0	Z	Z	Z	Z	Z	Z	Z	Z	C
1	0	0	Z	Z	Z	Z	Z	Z	Z	Z	C
# Pulse with enable and output
1	0	1	Z	Z	Z	Z	0	1	0	0	C
1	0	1	Z	Z	Z	Z	0	1	0	1	C
# Load data
0	1	0	1	1	0	0	1	1	0	0	C
0	0	1	Z	Z	Z	Z	1	1	0	0	C
# Pulse not enabled
0	0	1	Z	Z	Z	Z	1	1	0	0	C
0	0	1	Z	Z	Z	Z	1	1	0	0	C
# Check Overflow
1	0	1	Z	Z	Z	Z	1	1	0	1	C
1	0	1	Z	Z	Z	Z	1	1	1	0	C
1	0	1	Z	Z	Z	Z	1	1	1	1	C
1	0	1	Z	Z	Z	Z	0	0	0	0	C
*/
