// Digital circuit 3_1-4_byte_ram.dig as structural Verilog
module _3_1_4_byte_ram (
  input  C,
  input  D_0,
  input  D_1,
  input  D_2,
  input  D_3,
  input  D_4,
  input  D_5,
  input  D_6,
  input  D_7,
  input  W,
  input  R,
  input  A_0,
  input  A_1,
  output O_0,
  output O_1,
  output O_2,
  output O_3,
  output O_4,
  output O_5,
  output O_6,
  output O_7
);

  wire [7:0] demultiplexer_1_out_0, demultiplexer_1_out_1, demultiplexer_1_out_2, demultiplexer_1_out_3;

  Demultiplexer #(.Selector_Bits(2)) demultiplexer_1 (
    .out_0(demultiplexer_1_out_0[0]), .out_1(demultiplexer_1_out_1[0]), .out_2(demultiplexer_1_out_2[0]),
    .out_3(demultiplexer_1_out_3[0]));  // open: sel, in
  Multiplexer #(.Selector_Bits(2), .Bits(8)) multiplexer_1 (
    .in_0(demultiplexer_1_out_0), .in_1(demultiplexer_1_out_1), .in_2(demultiplexer_1_out_2),
    .in_3(demultiplexer_1_out_3));  // open: sel, out
  Driver #(.Bits(8)) driver_1 ();  // open: in, en, out
  Register #(.Bits(8)) register_1 ();  // open: D, C, en, Q
  Register #(.Bits(8)) register_2 ();  // open: D, C, en, Q
  Register #(.Bits(8)) register_3 ();  // open: D, C, en, Q
  Register #(.Bits(8)) register_4 ();  // open: D, C, en, Q
  // Pins of 1 and 8 bits meet at demultiplexer_1_out_0
  // Pins of 1 and 8 bits meet at demultiplexer_1_out_1
  // Pins of 1 and 8 bits meet at demultiplexer_1_out_2
  // Pins of 1 and 8 bits meet at demultiplexer_1_out_3

  assign O_0 = D_0;
  assign O_1 = D_1;
  assign O_2 = D_2;
  assign O_3 = D_3;
  assign O_4 = D_4;
  assign O_5 = D_5;
  assign O_6 = D_6;
  assign O_7 = D_7;

  // Notes on the sheet:
  //   4 Byte Ram
endmodule

/* Test case 4 byte ram_test:
W	R	A_1	A_0	D_7	D_6	D_5	D_4	D_3	D_2	D_1	D_0	O_7	O_6	O_5	O_4	O_3	O_2	O_1	O_0	C
# No Read/Write does nothing
0	0	X	X	X	X	X	X	X	X	X	X	X	X	X	X	X	X	X	X	C
# Read registers before write
0	1	0	0	Z	Z	Z	Z	Z	Z	Z	Z	0	0	0	0	0	0	0	0	C
0	1	0	1	Z	Z	Z	Z	Z	Z	Z	Z	0	0	0	0	0	0	0	0	C
0	1	1	0	Z	Z	Z	Z	Z	Z	Z	Z	0	0	0	0	0	0	0	0	C
0	1	1	1	Z	Z	Z	Z	Z	Z	Z	Z	0	0	0	0	0	0	0	0	C
# Write to registers
1	0	0	0	0	0	0	1	0	0	0	1	0	0	0	1	0	0	0	1	C
1	0	0	1	0	0	1	0	0	0	1	0	0	0	1	0	0	0	1	0	C
1	0	1	0	0	1	0	0	0	1	0	0	0	1	0	0	0	1	0	0	C
1	0	1	1	1	0	0	0	1	0	0	0	1	0	0	0	1	0	0	0	C
# Read registers after write
0	1	0	0	Z	Z	Z	Z	Z	Z	Z	Z	0	0	0	1	0	0	0	1	C
0	1	0	1	Z	Z	Z	Z	Z	Z	Z	Z	0	0	1	0	0	0	1	0	C
0	1	1	0	Z	Z	Z	Z	Z	Z	Z	Z	0	1	0	0	0	1	0	0	C
0	1	1	1	Z	Z	Z	Z	Z	Z	Z	Z	1	0	0	0	1	0	0	0	C
*/
