// Digital circuit 4-plex-input_output_selector.dig as structural Verilog
module _4_plex_input_output_selector (
  input  D_0,
  input  D_1,
  input  D_2,
  input  D_3,
  input  si_0,
  input  si_1,
  input  so_0,
  input  so_1,
  output O_0,
  output O_1,
  output O_2,
  output O_3
);


  // Notes on the sheet:
  //   plexer input output
endmodule

/* Test case plexer input output_test:
			si_1	si_0	D_3	D_2	D_1	D_0	so_1	so_0	O_3	O_2	O_1	O_0
loop(a, 4)
	loop(b, 4)
		loop(c,16)
			bits(2,a)	bits(4,c)			bits(2,b)	bits(4,((c>>a)&1)<<b)
		end loop
	end loop
end loop
*/
