// Digital circuit 3-comparator.dig as structural Verilog
module _3_comparator (
  input  o_0,
  input  o_1,
  input  o_2,
  input  [7:0] A,
  input  [7:0] B,
  output O
);

  Multiplexer #(.Selector_Bits(3)) multiplexer_1 ();  // open: sel, in_0, in_1, in_2, in_3, in_4, in_5, in_6, in_7, out

  // Notes on the sheet:
  //   Comparator
endmodule

/* Test case comparator_test:
o_2	o_1	o_0	A	B	O
# Never
0	0	0	0	0	0
0	0	0	10	10	0
0	0	0	10	11	0
0	0	0	11	10	0

# ==
0	0	1	0	0	1
0	0	1	10	10	1
0	0	1	10	11	0
0	0	1	11	10	0

# <
0	1	0	0	0	0
0	1	0	10	10	0
0	1	0	10	11	1
0	1	0	11	10	0

# <=
0	1	1	0	0	1
0	1	1	10	10	1
0	1	1	10	11	1
0	1	1	11	10	0

# Always
1	0	0	0	0	1
1	0	0	10	10	1
1	0	0	10	11	1
1	0	0	11	10	1

# !=
1	0	1	0	0	0
1	0	1	10	10	0
1	0	1	10	11	1
1	0	1	11	10	1

# >=
1	1	0	0	0	1
1	1	0	10	10	1
1	1	0	10	11	0
1	1	0	11	10	1

# >
1	1	1	0	0	0
1	1	1	10	10	0
1	1	1	10	11	0
1	1	1	11	10	1
*/
