// Digital circuit esap-alu.dig as structural Verilog
module esap_alu (
  input  d_0,
  input  d_1,
  input  d_2,
  input  d_3,
  input  d_4,
  input  d_5,
  input  d_6,
  input  d_7,
  input  sub,
  input  clk,
  input  A_i,
  input  A_o,
  input  B_i,
  input  B_o,
  input  ALU_o,
  output o_0,
  output o_1,
  output o_2,
  output o_3,
  output o_4,
  output o_5,
  output o_6,
  output o_7
);

  wire [7:0] A_q, add_1_s, B_q, xor_1_out;

  assign xor_1_out = B_q ^ {8{sub}};  // XOr xor_1, 8 bits wide
  Register #(.Bits(8)) A (.D({d_7, d_6, d_5, d_4, d_3, d_2, d_1, d_0}), .C(clk), .en(A_i), .Q(A_q));
  Register #(.Bits(8)) B (.D({d_7, d_6, d_5, d_4, d_3, d_2, d_1, d_0}), .C(clk), .en(B_i), .Q(B_q));
  Add #(.Bits(8)) add_1 (.a(A_q), .b(xor_1_out), .c_i(sub), .s(add_1_s));  // open: c_o
  assign {d_7, d_6, d_5, d_4, d_3, d_2, d_1, d_0} = ~A_o ? A_q : 8'bz;  // DriverInvSel driverinvsel_1
  assign {d_7, d_6, d_5, d_4, d_3, d_2, d_1, d_0} = ~B_o ? B_q : 8'bz;  // DriverInvSel driverinvsel_2
  assign {d_7, d_6, d_5, d_4, d_3, d_2, d_1, d_0} = ~ALU_o ? add_1_s : 8'bz;  // DriverInvSel driverinvsel_3

  assign o_0 = d_0;
  assign o_1 = d_1;
  assign o_2 = d_2;
  assign o_3 = d_3;
  assign o_4 = d_4;
  assign o_5 = d_5;
  assign o_6 = d_6;
  assign o_7 = d_7;

  // Notes on the sheet:
  //   ALU
endmodule

/* Test case alu_test:
		sub	a_7	a_6	a_5	a_4	a_3	a_2	a_1	a_0	b_7	b_6	b_5	b_4	b_3	b_2	b_1	b_0	o_7	o_6	o_5	o_4	o_3	o_2	o_1	o_0
loop(a, 128)
	loop(b, 128)
		0	bits(8,a)							bits(8,b)							bits(8,a+b)				
		1	bits(8,a)							bits(8,b)							bits(8,a-b)
	end loop
end loop	
*/
