// Digital circuit full_adder_4_bit.dig as structural Verilog
module full_adder_4_bit (
  input  C_in,
  input  A_0,
  input  A_1,
  input  A_2,
  input  A_3,
  input  B_0,
  input  B_1,
  input  B_2,
  input  B_3,
  output S_0,
  output S_1,
  output S_2,
  output S_3,
  output C_out
);

  wire and_1_out, and_2_out, and_3_out, and_4_out, and_5_out, and_6_out, and_7_out, and_8_out, or_1_out,
       or_2_out, or_3_out, xor_1_out, xor_2_out, xor_3_out, xor_4_out;

  xor xor_1 (xor_1_out, A_0, B_0);
  xor xor_2 (xor_2_out, A_1, B_1);
  xor xor_3 (xor_3_out, A_2, B_2);
  xor xor_4 (xor_4_out, A_3, B_3);
  xor xor_5 (S_0, xor_1_out, C_in);
  and and_1 (and_1_out, xor_1_out, C_in);
  and and_2 (and_2_out, A_0, B_0);
  xor xor_6 (S_1, xor_2_out, or_1_out);
  and and_3 (and_3_out, xor_2_out, or_1_out);
  and and_4 (and_4_out, A_1, B_1);
  xor xor_7 (S_2, xor_3_out, or_2_out);
  and and_5 (and_5_out, xor_3_out, or_2_out);
  and and_6 (and_6_out, A_2, B_2);
  xor xor_8 (S_3, xor_4_out, or_3_out);
  and and_7 (and_7_out, xor_4_out, or_3_out);
  and and_8 (and_8_out, A_3, B_3);
  or or_1 (or_1_out, and_1_out, and_2_out);
  or or_2 (or_2_out, and_3_out, and_4_out);
  or or_3 (or_3_out, and_5_out, and_6_out);
  or or_4 (C_out, and_7_out, and_8_out);

  // Notes on the sheet:
  //   4 bit Full Adder
endmodule

/* Test case 4 bit full adder_test:
		C_in	A_3	A_2	A_1	A_0	B_3	B_2	B_1	B_0	C_out	S_3	S_2	S_1	S_0
loop(a,15)
	loop(b,15)
		0	bits(4,a)			bits(4,b)			bits(5,a+b)	
		1	bits(4,a)			bits(4,b)			bits(5,a+b+1)
	end loop
end loop
*/
