// Digital circuit half_adder.dig as structural Verilog
module half_adder (
  input  A,
  input  B,
  output S,
  output C
);

  xor xor_1 (S, A, B);
  and and_1 (C, A, B);

  // Notes on the sheet:
  //   Half Adder
endmodule

/* Test case half adder_test:
A	B	S	C
0	0	0	0
0	1	1	0
1	0	1	0
1	1	0	1
*/
