// Digital circuit half_adder_with_pla.dig as structural Verilog
module half_adder_with_pla (
  input  A,
  input  B,
  output S,
  output C
);

  wire and_1_out, and_2_out, and_3_out;

  and and_1 (and_1_out, ~A, ~B);  // And
  and and_2 (and_2_out, A, ~B);  // And
  and and_3 (and_3_out, ~A, B);  // And
  and and_4 (C, A, B);
  or or_1 (S, and_2_out, and_3_out);

  // Notes on the sheet:
  //   Half Adder with PLA
endmodule

/* Test case half adder_test:
A	B	S	C
0	0	0	0
0	1	1	0
1	0	1	0
1	1	0	1
*/
