// Digital circuit adder_flags_register.dig as structural Verilog
module adder_flags_register (
  input  A_0,
  input  A_1,
  input  sub,
  input  B_0,
  input  A_2,
  input  A_3,
  input  A_4,
  input  A_5,
  input  A_6,
  input  A_7,
  input  B_1,
  input  B_2,
  input  B_3,
  input  B_4,
  input  B_5,
  input  B_6,
  input  B_7,
  input  C,
  input  flag,
  output Z_flag,
  output S_flag,
  output C_flag
);

  wire [2:0] add_1_s_2;
  wire [6:0] add_1_s;
  wire [7:0] xor_1_out;

  assign xor_1_out = {B_7, B_6, B_5, B_4, B_3, B_2, B_1, B_0} ^ {8{sub}};  // XOr xor_1, 8 bits wide
  Add #(.Bits(8)) add_1 (
    .a({A_7, A_6, A_5, A_4, A_3, A_2, A_1, A_0}), .b(xor_1_out), .c_i(sub), .s({add_1_s_2[1], add_1_s}),
    .c_o(add_1_s_2[2]));
  nor nor_1 (add_1_s_2[0], add_1_s[0], add_1_s[1], add_1_s[2], add_1_s[3], add_1_s[4], add_1_s[5], add_1_s[6], add_1_s_2[1]);
  Register #(.Bits(3)) u_Flag (.D(add_1_s_2), .C(C), .en(flag), .Q({C_flag, S_flag, Z_flag}));

  // Notes on the sheet:
  //   Flags Register
endmodule

/* Test case flags register_test:
A_7	A_6	A_5	A_4	A_3	A_2	A_1	A_0	B_7	B_6	B_5	B_4	B_3	B_2	B_1	B_0	sub	flag	Z_flag	S_flag	C_flag	C
# Register stays clear when no clock or enable
0	0	0	0	0	0	0	0	0	0	0	0	0	0	0	0	0	0	0	0	0	0
0	0	0	0	0	0	0	0	0	0	0	0	0	0	0	0	0	0	0	0	0	0
1	1	1	1	1	1	1	1	1	1	1	1	1	1	1	1	0	0	0	0	0	0
1	1	1	1	1	1	1	1	1	1	1	1	1	1	1	1	0	0	0	0	0	0
# 0 + 0 results in Z
0	0	0	0	0	0	0	0	0	0	0	0	0	0	0	0	0	1	1	0	0	C
# 1 + 0 results in no flag
0	0	0	0	0	0	0	1	0	0	0	0	0	0	0	1	0	1	0	0	0	C
# 1 - 1 results in Z and C
0	0	0	0	0	0	0	1	0	0	0	0	0	0	0	1	1	1	1	0	1	C
# Register stays unchanged when no enable 
0	0	0	0	0	0	0	0	0	0	0	0	0	0	0	0	0	0	1	0	1	C
# 255 + 1 results in Z and C
1	1	1	1	1	1	1	1	0	0	0	0	0	0	0	1	0	1	1	0	1	C
# Register stays unchanged when no enable
0	0	0	0	0	0	0	0	0	0	0	0	0	0	0	0	1	0	1	0	1	C
# 255 - 1 results in S and C
1	1	1	1	1	1	1	1	0	0	0	0	0	0	0	1	1	1	0	1	1	C
# Register stays unchanged when no enable
0	0	0	0	0	0	0	0	0	0	0	0	0	0	0	0	1	0	0	1	1	C
# 126 + 1 results in no flags 
0	1	1	1	1	1	1	0	0	0	0	0	0	0	0	1	0	1	0	0	0	C
# 126 + 2 results in S flag 
0	1	1	1	1	1	1	0	0	0	0	0	0	0	1	0	0	1	0	1	0	C
# 85 + 170 results in S flag
0	1	0	1	0	1	0	1	1	0	1	0	1	0	1	0	0	1	0	1	0	C
# 85 - 170 results in S and
0	1	0	1	0	1	0	1	1	0	1	0	1	0	1	0	1	1	0	1	0	C
*/
