// Digital circuit instruction_register_and_control_logic_with_flags.dig as structural Verilog
module instruction_register_and_control_logic_with_flags (
  input  D_0,
  input  C,
  input  D_1,
  input  D_2,
  input  D_3,
  input  D_4,
  input  D_5,
  input  D_6,
  input  D_7,
  input  instruction_i,
  input  instruction_o,
  input  Z_flag,
  input  S_flag,
  input  C_flag,
  output O_0,
  output O_1,
  output O_2,
  output O_3,
  output O_4,
  output O_5,
  output O_6,
  output O_7,
  output SGN,
  output ORI,
  output SUB,
  output ALU,
  output BRO,
  output BRI,
  output ARO,
  output ARI,
  output PCO,
  output PCI,
  output PCE,
  output HLT,
  output ADR,
  output RMI,
  output RMO,
  output IRI,
  output IRO,
  output FLG
);

  wire [1:0] counter_1_out;
  wire [7:0] Instruction_q;

  Register #(.Bits(8)) Instruction (
    .D({D_7, D_6, D_5, D_4, D_3, D_2, D_1, D_0}), .C(C), .en(instruction_i), .Q(Instruction_q));
  Counter #(.Bits(2)) counter_1 (.en(1'b1), .C(C), .clr(1'b0), .out(counter_1_out));  // open: ovf
  assign {D_7, D_6, D_5, D_4, D_3, D_2, D_1, D_0} = instruction_o ? {4'b0000, Instruction_q[3:0]} : 8'bz;  // Driver driver_1
  LookUpTable #(.Bits(18)) lookuptable_1 (
    .in0(counter_1_out[0]), .in1(counter_1_out[1]), .in2(Instruction_q[4]), .in3(Instruction_q[5]),
    .in4(Instruction_q[6]), .in5(Instruction_q[7]), .in6(Z_flag), .in7(S_flag), .in8(C_flag),
    .out({HLT, ADR, RMI, RMO, FLG, IRO, IRI, ORI, SGN, SUB, ALU, BRO, BRI, ARO, ARI, PCO, PCE, PCI}));

  assign O_0 = D_0;
  assign O_1 = D_1;
  assign O_2 = D_2;
  assign O_3 = D_3;
  assign O_4 = D_4;
  assign O_5 = D_5;
  assign O_6 = D_6;
  assign O_7 = D_7;

  // Notes on the sheet:
  //   Instruction Register, Control Logic with Flag Input
  //   contents of lookuptable_1 (hex, n*v repeats v):
  //   10004,4802,0,0,10004,4802,11000,4008,10004,4802,1008,0,10004,4802
  //   ,11000,4020,10004,4802,1020,0,10004,4802,11000,8010,10004,4802
  //   ,11000,8040,10004,4802,2000,88,10004,4802,2100,188,10004,4802
  //   ,1001,0,10004,4802,0,0,10004,4802,0,0,10004,4802,0,0,10004,4802
  //   ,11000,4400,10004,4802,11000,4600,10004,4802,20000,0,10004,4802
  //   ,0,0,10004,4802,11000,4008,10004,4802,1008,0,10004,4802,11000
  //   ,4020,10004,4802,1020,0,10004,4802,11000,8010,10004,4802,11000
  //   ,8040,10004,4802,2000,88,10004,4802,2100,188,10004,4802,1001,0
  //   ,10004,4802,0,0,10004,4802,0,0,10004,4802,0,0,10004,4802,11000
  //   ,4400,10004,4802,11000,4600,10004,4802,20000,0,10004,4802,0,0
  //   ,10004,4802,11000,4008,10004,4802,1008,0,10004,4802,11000,4020
  //   ,10004,4802,1020,0,10004,4802,11000,8010,10004,4802,11000,8040
  //   ,10004,4802,2000,88,10004,4802,2100,188,10004,4802,1001,0,10004
  //   ,4802,0,0,10004,4802,0,0,10004,4802,0,0,10004,4802,11000,4400
  //   ,10004,4802,11000,4600,10004,4802,20000,0,10004,4802,0,0,10004
  //   ,4802,11000,4008,10004,4802,1008,0,10004,4802,11000,4020,10004
  //   ,4802,1020,0,10004,4802,11000,8010,10004,4802,11000,8040,10004
  //   ,4802,2000,88,10004,4802,2100,188,10004,4802,1001,0,10004,4802
  //   ,0,0,10004,4802,0,0,10004,4802,0,0,10004,4802,11000,4400,10004
  //   ,4802,11000,4600,10004,4802,20000,0,10004,4802,0,0,10004,4802
  //   ,11000,4008,10004,4802,1008,0,10004,4802,11000,4020,10004,4802
  //   ,1020,0,10004,4802,11000,8010,10004,4802,11000,8040,10004,4802
  //   ,2000,88,10004,4802,2100,188,10004,4802,1001,0,10004,4802,0,0
  //   ,10004,4802,0,0,10004,4802,0,0,10004,4802,11000,4400,10004,4802
  //   ,11000,4600,10004,4802,20000,0,10004,4802,0,0,10004,4802,11000
  //   ,4008,10004,4802,1008,0,10004,4802,11000,4020,10004,4802,1020
  //   ,0,10004,4802,11000,8010,10004,4802,11000,8040,10004,4802,2000
  //   ,88,10004,4802,2100,188,10004,4802,1001,0,10004,4802,0,0,10004
  //   ,4802,0,0,10004,4802,0,0,10004,4802,11000,4400,10004,4802,11000
  //   ,4600,10004,4802,20000,0,10004,4802,0,0,10004,4802,11000,4008
  //   ,10004,4802,1008,0,10004,4802,11000,4020,10004,4802,1020,0,10004
  //   ,4802,11000,8010,10004,4802,11000,8040,10004,4802,2000,88,10004
  //   ,4802,2100,188,10004,4802,1001,0,10004,4802,0,0,10004,4802,0,0
  //   ,10004,4802,0,0,10004,4802,11000,4400,10004,4802,11000,4600,10004
  //   ,4802,20000,0,10004,4802,0,0,10004,4802,11000,4008,10004,4802
  //   ,1008,0,10004,4802,11000,4020,10004,4802,1020,0,10004,4802,11000
  //   ,8010,10004,4802,11000,8040,10004,4802,2000,88,10004,4802,2100
  //   ,188,10004,4802,1001,0,10004,4802,0,0,10004,4802,0,0,10004,4802
  //   ,0,0,10004,4802,11000,4400,10004,4802,11000,4600,10004,4802,20000
endmodule

/* Test case Control Logic with Flag_Test:
instruction_i		D_7	D_6	D_5	D_4	HLT	ADR	RMI	RMO	FLG	IRO	IRI	ORI	SGN	SUB	ALU	BRO	BRI	ARO	ARI	PCO	PCE	PCI	C
# NOOP																								
0		0	0	0	0	0	1	0	0	0	0	0	0	0	0	0	0	0	0	0	1	0	0	0
0		0	0	0	0	0	0	0	1	0	0	1	0	0	0	0	0	0	0	0	0	1	0	C
0		0	0	0	0	0	0	0	0	0	0	0	0	0	0	0	0	0	0	0	0	0	0	C
0		0	0	0	0	0	0	0	0	0	0	0	0	0	0	0	0	0	0	0	0	0	0	C
# LDAR																								
1		0	0	0	1	0	1	0	0	0	0	0	0	0	0	0	0	0	0	0	1	0	0	C
0		0	0	0	0	0	0	0	1	0	0	1	0	0	0	0	0	0	0	0	0	1	0	C
0		0	0	0	0	0	1	0	0	0	1	0	0	0	0	0	0	0	0	0	0	0	0	C
0		0	0	0	0	0	0	0	1	0	0	0	0	0	0	0	0	0	0	1	0	0	0	C
# LDAD																								
1		0	0	1	0	0	1	0	0	0	0	0	0	0	0	0	0	0	0	0	1	0	0	C
0		0	0	0	0	0	0	0	1	0	0	1	0	0	0	0	0	0	0	0	0	1	0	C
0		0	0	0	0	0	0	0	0	0	1	0	0	0	0	0	0	0	0	1	0	0	0	C
0		0	0	0	0	0	0	0	0	0	0	0	0	0	0	0	0	0	0	0	0	0	0	C
# LDBR																								
1		0	0	1	1	0	1	0	0	0	0	0	0	0	0	0	0	0	0	0	1	0	0	C
0		0	0	0	0	0	0	0	1	0	0	1	0	0	0	0	0	0	0	0	0	1	0	C
0		0	0	0	0	0	1	0	0	0	1	0	0	0	0	0	0	0	0	0	0	0	0	C
0		0	0	0	0	0	0	0	1	0	0	0	0	0	0	0	0	1	0	0	0	0	0	C
# LDBD																								
1		0	1	0	0	0	1	0	0	0	0	0	0	0	0	0	0	0	0	0	1	0	0	C
0		0	0	0	0	0	0	0	1	0	0	1	0	0	0	0	0	0	0	0	0	1	0	C
0		0	0	0	0	0	0	0	0	0	1	0	0	0	0	0	0	1	0	0	0	0	0	C
0		0	0	0	0	0	0	0	0	0	0	0	0	0	0	0	0	0	0	0	0	0	0	C
# SAVA																								
1		0	1	0	1	0	1	0	0	0	0	0	0	0	0	0	0	0	0	0	1	0	0	C
0		0	0	0	0	0	0	0	1	0	0	1	0	0	0	0	0	0	0	0	0	1	0	C
0		0	0	0	0	0	1	0	0	0	1	0	0	0	0	0	0	0	0	0	0	0	0	C
0		0	0	0	0	0	0	1	0	0	0	0	0	0	0	0	0	0	1	0	0	0	0	C
# SAVB																								
1		0	1	1	0	0	1	0	0	0	0	0	0	0	0	0	0	0	0	0	1	0	0	C
0		0	0	0	0	0	0	0	1	0	0	1	0	0	0	0	0	0	0	0	0	1	0	C
0		0	0	0	0	0	1	0	0	0	1	0	0	0	0	0	0	0	0	0	0	0	0	C
0		0	0	0	0	0	0	1	0	0	0	0	0	0	0	0	1	0	0	0	0	0	0	C
# ADAB																								
1		0	1	1	1	0	1	0	0	0	0	0	0	0	0	0	0	0	0	0	1	0	0	C
0		0	0	0	0	0	0	0	1	0	0	1	0	0	0	0	0	0	0	0	0	1	0	C
0		0	0	0	0	0	0	0	0	1	0	0	0	0	0	0	0	0	0	0	0	0	0	C
0		0	0	0	0	0	0	0	0	0	0	0	0	0	0	1	0	0	0	1	0	0	0	C
# SUAB																								
1		1	0	0	0	0	1	0	0	0	0	0	0	0	0	0	0	0	0	0	1	0	0	C
0		0	0	0	0	0	0	0	1	0	0	1	0	0	0	0	0	0	0	0	0	1	0	C
0		0	0	0	0	0	0	0	0	1	0	0	0	0	1	0	0	0	0	0	0	0	0	C
0		0	0	0	0	0	0	0	0	0	0	0	0	0	1	1	0	0	0	1	0	0	0	C
# JMPA																								
1		1	0	0	1	0	1	0	0	0	0	0	0	0	0	0	0	0	0	0	1	0	0	C
0		0	0	0	0	0	0	0	1	0	0	1	0	0	0	0	0	0	0	0	0	1	0	C
0		0	0	0	0	0	0	0	0	0	1	0	0	0	0	0	0	0	0	0	0	0	1	C
0		0	0	0	0	0	0	0	0	0	0	0	0	0	0	0	0	0	0	0	0	0	0	C
																								
# JMPZ																								
1		1	0	1	0	0	1	0	0	0	0	0	0	0	0	0	0	0	0	0	1	0	0	C
0		0	0	0	0	0	0	0	1	0	0	1	0	0	0	0	0	0	0	0	0	1	0	C
0		0	0	0	0	0	0	0	0	0	0	0	0	0	0	0	0	0	0	0	0	0	0	C
0		0	0	0	0	0	0	0	0	0	0	0	0	0	0	0	0	0	0	0	0	0	0	C
# JMPS																								
1		1	0	1	1	0	1	0	0	0	0	0	0	0	0	0	0	0	0	0	1	0	0	C
0		0	0	0	0	0	0	0	1	0	0	1	0	0	0	0	0	0	0	0	0	1	0	C
0		0	0	0	0	0	0	0	0	0	0	0	0	0	0	0	0	0	0	0	0	0	0	C
0		0	0	0	0	0	0	0	0	0	0	0	0	0	0	0	0	0	0	0	0	0	0	C
# JMPC																								
1		1	1	0	0	0	1	0	0	0	0	0	0	0	0	0	0	0	0	0	1	0	0	C
0		0	0	0	0	0	0	0	1	0	0	1	0	0	0	0	0	0	0	0	0	1	0	C
0		0	0	0	0	0	0	0	0	0	0	0	0	0	0	0	0	0	0	0	0	0	0	C
0		0	0	0	0	0	0	0	0	0	0	0	0	0	0	0	0	0	0	0	0	0	0	C
# OUTU																								
1		1	1	0	1	0	1	0	0	0	0	0	0	0	0	0	0	0	0	0	1	0	0	C
0		0	0	0	0	0	0	0	1	0	0	1	0	0	0	0	0	0	0	0	0	1	0	C
0		0	0	0	0	0	1	0	0	0	1	0	0	0	0	0	0	0	0	0	0	0	0	C
0		0	0	0	0	0	0	0	1	0	0	0	1	0	0	0	0	0	0	0	0	0	0	C
# OUTS																								
1		1	1	1	0	0	1	0	0	0	0	0	0	0	0	0	0	0	0	0	1	0	0	C
0		0	0	0	0	0	0	0	1	0	0	1	0	0	0	0	0	0	0	0	0	1	0	C
0		0	0	0	0	0	1	0	0	0	1	0	0	0	0	0	0	0	0	0	0	0	0	C
0		0	0	0	0	0	0	0	1	0	0	0	1	1	0	0	0	0	0	0	0	0	0	C
# HALT																								
1		1	1	1	1	0	1	0	0	0	0	0	0	0	0	0	0	0	0	0	1	0	0	C
0		0	0	0	0	0	0	0	1	0	0	1	0	0	0	0	0	0	0	0	0	1	0	C
0		0	0	0	0	1	0	0	0	0	0	0	0	0	0	0	0	0	0	0	0	0	0	C
0		0	0	0	0	0	0	0	0	0	0	0	0	0	0	0	0	0	0	0	0	0	0	C
*/
