// Digital circuit control-logic.dig as structural Verilog
module control_logic (
  input  D_0,
  input  C,
  input  D_1,
  input  D_2,
  input  D_3,
  input  D_4,
  input  D_5,
  input  D_6,
  input  D_7,
  input  instruction_i,
  input  instruction_o,
  output O_0,
  output O_1,
  output O_2,
  output O_3,
  output O_4,
  output O_5,
  output O_6,
  output O_7,
  output SGN,
  output ORI,
  output SUB,
  output ALU,
  output BRO,
  output BRI,
  output ARO,
  output ARI,
  output PCO,
  output PCI,
  output PCE,
  output HLT,
  output ADR,
  output RMI,
  output RMO,
  output IRI,
  output IRO
);

  wire [2:0] add_1_s, Micro_q, multiplexer_1_out;
  wire [7:0] Instruction_q;

  Register #(.Bits(8)) Instruction (
    .D({D_7, D_6, D_5, D_4, D_3, D_2, D_1, D_0}), .C(C), .en(instruction_i), .Q(Instruction_q));
  Multiplexer #(.Bits(3)) multiplexer_1 (.sel(add_1_s[2]), .in_0(add_1_s), .in_1(3'b000), .out(multiplexer_1_out));
  Register #(.Bits(3)) Micro (.D(multiplexer_1_out), .C(C), .en(1'b1), .Q(Micro_q));
  assign {D_7, D_6, D_5, D_4, D_3, D_2, D_1, D_0} = instruction_o ? {4'b0000, Instruction_q[3:0]} : 8'bz;  // Driver driver_1
  Add #(.Bits(3)) add_1 (.a(Micro_q), .b(3'b001), .c_i(1'b0), .s(add_1_s));  // open: c_o
  LookUpTable #(.Bits(17)) lookuptable_1 (
    .in0(Micro_q[0]), .in1(Micro_q[1]), .in2(Instruction_q[4]), .in3(Instruction_q[5]),
    .in4(Instruction_q[6]), .in5(Instruction_q[7]),
    .out({IRO, IRI, RMO, RMI, ADR, HLT, PCE, PCI, PCO, ARI, ARO, BRI, BRO, ALU, SUB, ORI, SGN}));

  assign O_0 = D_0;
  assign O_1 = D_1;
  assign O_2 = D_2;
  assign O_3 = D_3;
  assign O_4 = D_4;
  assign O_5 = D_5;
  assign O_6 = D_6;
  assign O_7 = D_7;

  // Notes on the sheet:
  //   Instruction Register and Control Logic
  //   contents of lookuptable_1 (hex, n*v repeats v):
  //   1100,c400,0,0,1100,c400,11000,4080,1100,c400,10080,0,1100,c400
  //   ,11000,4020,1100,c400,10020,0,1100,c400,11000,2040,1100,c400,11000
  //   ,2010,1100,c400,88,0,1100,c400,8c,0,1100,c400,10200,0,1100,c400
  //   ,0,0,1100,c400,0,0,1100,c400,0,0,1100,c400,11000,4002,1100,c400
  //   ,11000,4003,1100,c400,800
endmodule

/* Test case Instruction Register_Test:
instruction_i	instruction_o	D_7	D_6	D_5	D_4	D_3	D_2	D_1	D_0	O_7	O_6	O_5	O_4	O_3	O_2	O_1	O_0	C
# Instruction Register Only Outputs 4 Lowest Significant Bits
1		0		0	1	0	1	0	1	0	1	0	1	0	1	0	1	0	1	C
0		0		0	0	0	0	0	0	0	0	0	0	0	0	0	0	0	0	C
0		1		Z	Z	Z	Z	Z	Z	Z	Z	0	0	0	0	0	1	0	1	C
1		0		1	0	1	0	1	0	1	0	1	0	1	0	1	0	1	0	C
0		0		0	0	0	0	0	0	0	0	0	0	0	0	0	0	0	0	C
0		1		Z	Z	Z	Z	Z	Z	Z	Z	0	0	0	0	1	0	1	0	C
*/

/* Test case Control Logic_Test:
instruction_i	D_7	D_6	D_5	D_4	IRO	IRI	RMO	RMI	ADR	HLT	PCE	PCI	PCO	ARI	ARO	BRI	BRO	ALU	SUB	ORI	SGN	C
# NOOP
0		0	0	0	0	0	0	0	0	1	0	0	0	1	0	0	0	0	0	0	0	0	0
0		0	0	0	0	0	1	1	0	0	0	1	0	0	0	0	0	0	0	0	0	0	C
0		0	0	0	0	0	0	0	0	0	0	0	0	0	0	0	0	0	0	0	0	0	C
0		0	0	0	0	0	0	0	0	0	0	0	0	0	0	0	0	0	0	0	0	0	C
# LDAR
1		0	0	0	1	0	0	0	0	1	0	0	0	1	0	0	0	0	0	0	0	0	C
0		0	0	0	0	0	1	1	0	0	0	1	0	0	0	0	0	0	0	0	0	0	C
0		0	0	0	0	1	0	0	0	1	0	0	0	0	0	0	0	0	0	0	0	0	C
0		0	0	0	0	0	0	1	0	0	0	0	0	0	1	0	0	0	0	0	0	0	C
# LDAD
1		0	0	1	0	0	0	0	0	1	0	0	0	1	0	0	0	0	0	0	0	0	C
0		0	0	0	0	0	1	1	0	0	0	1	0	0	0	0	0	0	0	0	0	0	C
0		0	0	0	0	1	0	0	0	0	0	0	0	0	1	0	0	0	0	0	0	0	C
0		0	0	0	0	0	0	0	0	0	0	0	0	0	0	0	0	0	0	0	0	0	C
# LDBR
1		0	0	1	1	0	0	0	0	1	0	0	0	1	0	0	0	0	0	0	0	0	C
0		0	0	0	0	0	1	1	0	0	0	1	0	0	0	0	0	0	0	0	0	0	C
0		0	0	0	0	1	0	0	0	1	0	0	0	0	0	0	0	0	0	0	0	0	C
0		0	0	0	0	0	0	1	0	0	0	0	0	0	0	0	1	0	0	0	0	0	C
# LDBD
1		0	1	0	0	0	0	0	0	1	0	0	0	1	0	0	0	0	0	0	0	0	C
0		0	0	0	0	0	1	1	0	0	0	1	0	0	0	0	0	0	0	0	0	0	C
0		0	0	0	0	1	0	0	0	0	0	0	0	0	0	0	1	0	0	0	0	0	C
0		0	0	0	0	0	0	0	0	0	0	0	0	0	0	0	0	0	0	0	0	0	C
# SAVA
1		0	1	0	1	0	0	0	0	1	0	0	0	1	0	0	0	0	0	0	0	0	C
0		0	0	0	0	0	1	1	0	0	0	1	0	0	0	0	0	0	0	0	0	0	C
0		0	0	0	0	1	0	0	0	1	0	0	0	0	0	0	0	0	0	0	0	0	C
0		0	0	0	0	0	0	0	1	0	0	0	0	0	0	1	0	0	0	0	0	0	C
# SAVB
1		0	1	1	0	0	0	0	0	1	0	0	0	1	0	0	0	0	0	0	0	0	C
0		0	0	0	0	0	1	1	0	0	0	1	0	0	0	0	0	0	0	0	0	0	C
0		0	0	0	0	1	0	0	0	1	0	0	0	0	0	0	0	0	0	0	0	0	C
0		0	0	0	0	0	0	0	1	0	0	0	0	0	0	0	0	1	0	0	0	0	C
# ADDB
1		0	1	1	1	0	0	0	0	1	0	0	0	1	0	0	0	0	0	0	0	0	C
0		0	0	0	0	0	1	1	0	0	0	1	0	0	0	0	0	0	0	0	0	0	C
0		0	0	0	0	0	0	0	0	0	0	0	0	0	1	0	0	0	1	0	0	0	C
0		0	0	0	0	0	0	0	0	0	0	0	0	0	0	0	0	0	0	0	0	0	C
# SUBB
1		1	0	0	0	0	0	0	0	1	0	0	0	1	0	0	0	0	0	0	0	0	C
0		0	0	0	0	0	1	1	0	0	0	1	0	0	0	0	0	0	0	0	0	0	C
0		0	0	0	0	0	0	0	0	0	0	0	0	0	1	0	0	0	1	1	0	0	C
0		0	0	0	0	0	0	0	0	0	0	0	0	0	0	0	0	0	0	0	0	0	C
# JUMP
1		1	0	0	1	0	0	0	0	1	0	0	0	1	0	0	0	0	0	0	0	0	C
0		0	0	0	0	0	1	1	0	0	0	1	0	0	0	0	0	0	0	0	0	0	C
0		0	0	0	0	1	0	0	0	0	0	0	1	0	0	0	0	0	0	0	0	0	C
0		0	0	0	0	0	0	0	0	0	0	0	0	0	0	0	0	0	0	0	0	0	C

# NOOP
1		1	0	1	0	0	0	0	0	1	0	0	0	1	0	0	0	0	0	0	0	0	C
0		0	0	0	0	0	1	1	0	0	0	1	0	0	0	0	0	0	0	0	0	0	C
0		0	0	0	0	0	0	0	0	0	0	0	0	0	0	0	0	0	0	0	0	0	C
0		0	0	0	0	0	0	0	0	0	0	0	0	0	0	0	0	0	0	0	0	0	C
# NOOP
1		1	0	1	1	0	0	0	0	1	0	0	0	1	0	0	0	0	0	0	0	0	C
0		0	0	0	0	0	1	1	0	0	0	1	0	0	0	0	0	0	0	0	0	0	C
0		0	0	0	0	0	0	0	0	0	0	0	0	0	0	0	0	0	0	0	0	0	C
0		0	0	0	0	0	0	0	0	0	0	0	0	0	0	0	0	0	0	0	0	0	C
# NOOP
1		1	1	0	0	0	0	0	0	1	0	0	0	1	0	0	0	0	0	0	0	0	C
0		0	0	0	0	0	1	1	0	0	0	1	0	0	0	0	0	0	0	0	0	0	C
0		0	0	0	0	0	0	0	0	0	0	0	0	0	0	0	0	0	0	0	0	0	C
0		0	0	0	0	0	0	0	0	0	0	0	0	0	0	0	0	0	0	0	0	0	C
# OUTU
1		1	1	0	1	0	0	0	0	1	0	0	0	1	0	0	0	0	0	0	0	0	C
0		0	0	0	0	0	1	1	0	0	0	1	0	0	0	0	0	0	0	0	0	0	C
0		0	0	0	0	1	0	0	0	1	0	0	0	0	0	0	0	0	0	0	0	0	C
0		0	0	0	0	0	0	1	0	0	0	0	0	0	0	0	0	0	0	0	1	0	C
# OUTS
1		1	1	1	0	0	0	0	0	1	0	0	0	1	0	0	0	0	0	0	0	0	C
0		0	0	0	0	0	1	1	0	0	0	1	0	0	0	0	0	0	0	0	0	0	C
0		0	0	0	0	1	0	0	0	1	0	0	0	0	0	0	0	0	0	0	0	0	C
0		0	0	0	0	0	0	1	0	0	0	0	0	0	0	0	0	0	0	0	1	1	C
# HALT
1		1	1	1	1	0	0	0	0	1	0	0	0	1	0	0	0	0	0	0	0	0	C
0		0	0	0	0	0	1	1	0	0	0	1	0	0	0	0	0	0	0	0	0	0	C
0		0	0	0	0	0	0	0	0	0	1	0	0	0	0	0	0	0	0	0	0	0	C
0		0	0	0	0	0	0	0	0	0	0	0	0	0	0	0	0	0	0	0	0	0	C
*/
