// Digital circuit instruction_register.dig as structural Verilog
module instruction_register (
  input  D_0,
  input  C,
  input  D_1,
  input  D_2,
  input  D_3,
  input  D_4,
  input  D_5,
  input  D_6,
  input  D_7,
  input  instruction_i,
  input  instruction_o,
  output O_0,
  output O_1,
  output O_2,
  output O_3,
  output O_4,
  output O_5,
  output O_6,
  output O_7
);

  wire [7:0] Instruction_q;

  Register #(.Bits(8)) Instruction (
    .D({D_7, D_6, D_5, D_4, D_3, D_2, D_1, D_0}), .C(C), .en(instruction_i), .Q(Instruction_q));
  assign {D_7, D_6, D_5, D_4, D_3, D_2, D_1, D_0} = instruction_o ? {4'b0000, Instruction_q[3:0]} : 8'bz;  // Driver driver_1

  assign O_0 = D_0;
  assign O_1 = D_1;
  assign O_2 = D_2;
  assign O_3 = D_3;
  assign O_4 = D_4;
  assign O_5 = D_5;
  assign O_6 = D_6;
  assign O_7 = D_7;

  // Notes on the sheet:
  //   Instruction Register
endmodule

/* Test case Instruction Register_Test:
instruction_i	instruction_o	D_7	D_6	D_5	D_4	D_3	D_2	D_1	D_0	O_7	O_6	O_5	O_4	O_3	O_2	O_1	O_0	C
# Instruction Register Only Outputs 4 Lowest Significant Bits
1		0		0	1	0	1	0	1	0	1	0	1	0	1	0	1	0	1	C
0		0		0	0	0	0	0	0	0	0	0	0	0	0	0	0	0	0	C
0		1		Z	Z	Z	Z	Z	Z	Z	Z	0	0	0	0	0	1	0	1	C
1		0		1	0	1	0	1	0	1	0	1	0	1	0	1	0	1	0	C
0		0		0	0	0	0	0	0	0	0	0	0	0	0	0	0	0	0	C
0		1		Z	Z	Z	Z	Z	Z	Z	Z	0	0	0	0	1	0	1	0	C
*/
