// Digital circuit alu_flags_register.dig as structural Verilog
module alu_flags_register (
  input  D_0,
  input  D_1,
  input  D_2,
  input  D_3,
  input  D_4,
  input  D_5,
  input  D_6,
  input  D_7,
  input  sub,
  input  C,
  input  A_i,
  input  A_o,
  input  B_i,
  input  B_o,
  input  ALU_o,
  output O_0,
  output O_1,
  output O_2,
  output O_3,
  output O_4,
  output O_5,
  output O_6,
  output O_7
);

  wire [7:0] A_q, add_1_s, B_q, xor_1_out;

  assign xor_1_out = B_q ^ {8{sub}};  // XOr xor_1, 8 bits wide
  Register #(.Bits(8)) A (.D({D_7, D_6, D_5, D_4, D_3, D_2, D_1, D_0}), .C(C), .en(A_i), .Q(A_q));
  Register #(.Bits(8)) B (.D({D_7, D_6, D_5, D_4, D_3, D_2, D_1, D_0}), .C(C), .en(B_i), .Q(B_q));
  Add #(.Bits(8)) add_1 (.a(A_q), .b(xor_1_out), .c_i(sub), .s(add_1_s));  // open: c_o
  assign {D_7, D_6, D_5, D_4, D_3, D_2, D_1, D_0} = A_o ? A_q : 8'bz;  // Driver driver_1
  assign {D_7, D_6, D_5, D_4, D_3, D_2, D_1, D_0} = B_o ? B_q : 8'bz;  // Driver driver_2
  assign {D_7, D_6, D_5, D_4, D_3, D_2, D_1, D_0} = ALU_o ? add_1_s : 8'bz;  // Driver driver_3

  assign O_0 = D_0;
  assign O_1 = D_1;
  assign O_2 = D_2;
  assign O_3 = D_3;
  assign O_4 = D_4;
  assign O_5 = D_5;
  assign O_6 = D_6;
  assign O_7 = D_7;

  // Notes on the sheet:
  //   Flags Register
endmodule

/* Test case flags register_test:
	A_i	A_o	B_i	B_o	ALU_o	sub	D_7	D_6	D_5	D_4	D_3	D_2	D_1	D_0	O_7	O_6	O_5	O_4	O_3	O_2	O_1	O_0	C
	0	0	0	0	0	0	0	0	0	0	0	0	0	0	0	0	0	0	0	0	0	0	C
	# Load 15 into A and Verify
	1	0	0	0	0	0	0	0	0	0	1	1	1	1	0	0	0	0	1	1	1	1	C
	0	1	0	0	0	0	Z	Z	Z	Z	Z	Z	Z	Z	0	0	0	0	1	1	1	1	C
	# Load 4 into B and Verify
	0	0	1	0	0	0	0	0	0	0	0	1	0	0	0	0	0	0	0	1	0	0	C
	0	0	0	1	0	0	Z	Z	Z	Z	Z	Z	Z	Z	0	0	0	0	0	1	0	0	C
	# Output Sum of A and B (15 + 4)
	0	0	0	0	1	0	Z	Z	Z	Z	Z	Z	Z	Z	0	0	0	1	0	0	1	1	C
	# Output Difference of A and B (15 - 4), Save in A, and Verify (note, after clock pulse, ALU otuput updates to the new A - B, thus it would be A - B - B)
	1	0	0	0	1	1	Z	Z	Z	Z	Z	Z	Z	Z	0	0	0	0	0	1	1	1	C
	0	1	0	0	0	0	Z	Z	Z	Z	Z	Z	Z	Z	0	0	0	0	1	0	1	1	C

# Add and Subtract Random Numbers
loop(a, 50)
	let r1 = random(255);
	let r2 = random(255);
	1	0	0	0	0	0	bits(8, r1)							bits(8, r1)							C
	0	0	1	0	0	0	bits(8, r2)							bits(8, r2)							C
	0	0	0	0	1	0	Z	Z	Z	Z	Z	Z	Z	Z	bits(8, r1+r2)							C
	0	0	0	0	1	1	Z	Z	Z	Z	Z	Z	Z	Z	bits(8, r1-r2)							C
end loop
*/
