// Digital circuit flags.dig as structural Verilog
module flags (
  input  D_0,
  input  D_1,
  input  D_2,
  input  D_3,
  input  D_4,
  input  D_5,
  input  D_6,
  input  D_7,
  input  Carry,
  output Z_flag,
  output S_flag,
  output C_flag
);

  nor nor_1 (Z_flag, D_0, D_1, D_2, D_3, D_4, D_5, D_6, D_7);

  assign C_flag = Carry;
  assign S_flag = D_7;

  // Notes on the sheet:
  //   Flags
endmodule

/* Test case flags_test:
D_7	D_6	D_5	D_4	D_3	D_2	D_1	D_0	Carry	Z_flag	S_flag	C_flag		
0	0	0	0	0	0	0	0	0	1	0	0	
0	0	0	0	0	0	0	0	1	1	0	1
1	0	0	0	0	0	0	0	0	0	1	0
1	0	0	0	0	0	0	0	1	0	1	1
0	1	0	1	0	1	0	1	0	0	0	0
0	1	0	1	0	1	0	1	1	0	0	1
1	0	1	0	1	0	1	0	0	0	1	0
1	0	1	0	1	0	1	0	1	0	1	1
*/
