// Digital circuit ram_register.dig as structural Verilog
module ram_register (
  input  C,
  input  D_3,
  input  D_2,
  input  D_1,
  input  D_0,
  input  RAM_i,
  input  RAM_o,
  input  REG_i,
  input  REG_o,
  input  A_1,
  input  A_0,
  output O_0,
  output O_1,
  output O_3,
  output O_2
);

  wire [3:0] register_1_q;

  RAMSinglePort #(.Bits(4)) ramsingleport_1 (.A({A_1, A_0}), .str(RAM_i), .C(C), .ld(RAM_o), .D({D_3, D_2, D_1, D_0}));
  Register #(.Bits(4)) register_1 (.D({D_3, D_2, D_1, D_0}), .C(C), .en(REG_i), .Q(register_1_q));
  assign {D_3, D_2, D_1, D_0} = REG_o ? register_1_q : 4'bz;  // Driver driver_1

  assign O_0 = D_0;
  assign O_1 = D_1;
  assign O_2 = D_2;
  assign O_3 = D_3;
endmodule

/* Test case ram register_test:
RAM_i	RAM_o	REG_i	REG_o	A_1	A_0	D_3	D_2	D_1	D_0	O_3	O_2	O_1	O_0	C
# Add data to RAM
1	0	0	0	0	0	0	0	0	1	0	0	0	1	C
1	0	0	0	0	1	1	0	0	0	1	0	0	0	C
# Verify data is in RAM
0	1	0	0	0	0	Z	Z	Z	Z	0	0	0	1	C
0	1	0	0	0	1	Z	Z	Z	Z	1	0	0	0	C
# Swap contents of address 0b00 and 0b01
0	1	1	0	0	0	Z	Z	Z	Z	0	0	0	1	C
1	0	0	1	1	0	Z	Z	Z	Z	0	0	0	1	C
0	1	1	0	0	1	Z	Z	Z	Z	1	0	0	0	C
1	0	0	1	0	0	Z	Z	Z	Z	1	0	0	0	C
0	1	1	0	1	0	Z	Z	Z	Z	0	0	0	1	C
1	0	0	1	0	1	Z	Z	Z	Z	0	0	0	1	C
# Verify data in RAM was swapped
0	1	0	0	0	0	Z	Z	Z	Z	1	0	0	0	C
0	1	0	0	0	1	Z	Z	Z	Z	0	0	0	1	C
*/
