// Digital circuit 1-2_and_2-4_decoders.dig as structural Verilog
module _1_2_and_2_4_decoders (
  input  \input ,
  input  input_a,
  input  input_b,
  output output_a,
  output output_b,
  output output_0,
  output output_1,
  output output_2,
  output output_3
);

  not not_1 (output_a, \input );
  and and_1 (output_0, ~input_a, ~input_b);  // And
  and and_2 (output_1, ~input_a, input_b);  // And
  and and_3 (output_2, input_a, ~input_b);  // And
  and and_4 (output_3, input_a, input_b);

  assign output_b = \input ;

  // Notes on the sheet:
  //   Single Bit Decoder
  //   Two Bit Decoder
endmodule

/* Test case 1 bit decoder_test:
input	output_a	output_b
0	1		0
1	0		1
*/

/* Test case 2 bit decoder_test:
input_a	input_b	output_0	output_1	output_2	output_3
0	0	1		0		0		0
0	1	0		1		0		0
1	0	0		0		1		0
1	1	0		0		0		1
*/
