// Digital circuit functional_completeness.dig as structural Verilog
module functional_completeness (
  input  in_a,
  input  in_b,
  input  in_c,
  input  in_d,
  input  in_f,
  input  in_e,
  input  in_g,
  input  in_h,
  input  in_i,
  input  in_j,
  input  in_k,
  input  in_l,
  input  in_m,
  input  in_n,
  output out_a,
  output out_b,
  output out_d,
  output out_c,
  output out_e,
  output out_f,
  output out_g,
  output out_h
);

  wire and_1_out, nand_1_out, nand_2_out, nand_3_out, nor_1_out, nor_2_out, nor_3_out, not_1_out, not_2_out,
       not_3_out, not_4_out, or_1_out;

  not not_1 (not_1_out, in_a);
  not not_2 (not_2_out, in_b);
  not not_3 (not_3_out, in_c);
  not not_4 (not_4_out, in_d);
  or or_1 (or_1_out, not_1_out, not_2_out);
  and and_1 (and_1_out, not_3_out, not_4_out);
  not not_5 (out_a, or_1_out);
  not not_6 (out_b, and_1_out);
  nor nor_1 (nor_1_out, in_g, in_h);
  nor nor_2 (nor_2_out, in_k, in_k);
  nor nor_3 (nor_3_out, in_l, in_l);
  nor nor_4 (out_c, in_e, in_e);
  nor nor_5 (out_e, nor_1_out, nor_1_out);
  nor nor_6 (out_g, nor_2_out, nor_3_out);
  nand nand_1 (nand_1_out, in_i, in_j);
  nand nand_2 (nand_2_out, in_m, in_m);
  nand nand_3 (nand_3_out, in_n, in_n);
  nand nand_4 (out_d, in_f, in_f);
  nand nand_5 (out_f, nand_1_out, nand_1_out);
  nand nand_6 (out_h, nand_2_out, nand_3_out);

  // Notes on the sheet:
  //   AND with OR and NOT Gates
  //   OR with ANDand NOT Gates
  //   NOT with NOR Gates
  //   OR with NOR Gates
  //   AND with NOR Gates
  //   NOT with NAND Gates
  //   AND with NAND Gates
  //   OR with NAND Gates
endmodule

/* Test case AND with OR_test:
in_a	in_b	out_a
0	0	0
0	1	0
1	0	0
1	1	1
*/

/* Test case OR with AND_test:
in_c	in_d	out_b
0	0	0
0	1	1
1	0	1
1	1	1
*/

/* Test case NOT with NOR_test:
in_e	out_c
0	1
1	0
*/

/* Test case OR with NOR_test:
in_g	in_h	out_e
0	0	0
0	1	1
1	0	1
1	1	1
*/

/* Test case AND with NOR_test:
in_k	in_l	out_g
0	0	0
0	1	0
1	0	0
1	1	1
*/

/* Test case NOT with NAND_test:
in_f	out_d
0	1
1	0
*/

/* Test case AND with NAND_test:
in_i	in_j	out_f
0	0	0
0	1	0
1	0	0
1	1	1
*/

/* Test case OR with NAND_test:
in_m	in_n	out_h
0	0	0
0	1	1
1	0	1
1	1	1
*/
