// Digital circuit programmable_logic_array.dig as structural Verilog
module programmable_logic_array (
  input  input_c,
  input  input_b,
  input  input_a,
  input  input_1,
  input  input_0,
  output output_a,
  output output_b,
  output output_c,
  output output_d,
  output output_0,
  output output_1,
  output output_2
);

  wire and_1_out, and_2_out, and_3_out, and_4_out, and_5_out, and_6_out, and_7_out, and_8_out, and_9_out,
       and_10_out, and_11_out, and_12_out;

  and and_1 (and_1_out, ~input_0, ~input_1);  // And
  and and_2 (and_2_out, input_0, ~input_1);  // And
  and and_3 (and_3_out, ~input_0, input_1);  // And
  and and_4 (and_4_out, input_0, input_1);
  and and_5 (and_5_out, ~input_a, ~input_b, ~input_c);  // And
  and and_6 (and_6_out, input_a, ~input_b, ~input_c);  // And
  and and_7 (and_7_out, ~input_a, input_b, ~input_c);  // And
  and and_8 (and_8_out, input_a, input_b, ~input_c);  // And
  and and_9 (and_9_out, ~input_a, ~input_b, input_c);  // And
  and and_10 (and_10_out, input_a, ~input_b, input_c);  // And
  and and_11 (and_11_out, ~input_a, input_b, input_c);  // And
  and and_12 (and_12_out, input_a, input_b, input_c);
  or or_1 (output_0, and_1_out, and_3_out, and_4_out);
  or or_2 (output_1, and_2_out, and_3_out);
  or or_3 (output_2, and_2_out, and_3_out, and_4_out);
  or or_4 (output_a, and_5_out, and_8_out, and_10_out, and_12_out);
  or or_5 (output_b, and_6_out, and_9_out, and_11_out);
  or or_6 (output_c, and_5_out, and_7_out, and_10_out, and_12_out);
  or or_7 (output_d, and_6_out, and_8_out, and_11_out);

  // Notes on the sheet:
  //   PLA Example 1
  //   PLA Example 2
endmodule

/* Test case pla example 1_test:
input_1	input_0	output_0	output_1	output_2
0	0	1		0		0
0	1	0		1		1
1	0	1		1		1
1	1	1		0		1
*/

/* Test case pla example 2_test:
input_c	input_b	input_a	output_a	output_b	output_c	output_d
0	0	0	1		0		1		0
0	0	1	0		1		0		1
0	1	0	0		0		1		0
0	1	1	1		0		0		1
1	0	0	0		1		0		0
1	0	1	1		0		1		0
1	1	0	0		1		0		1
1	1	1	1		0		1		0
*/
