// Digital circuit 1_bit_register.dig as structural Verilog
module _1_bit_register (
  input  Enable,
  input  Clock,
  input  D_0,
  output Q_0
);

  wire and_1_out, and_2_out, not_1_out, or_1_out;

  not not_1 (not_1_out, Enable);
  and and_1 (and_1_out, Q_0, not_1_out);
  and and_2 (and_2_out, Enable, D_0);
  or or_1 (or_1_out, and_1_out, and_2_out);
  D_FF d_ff_1 (.D(or_1_out), .C(Clock), .Q(Q_0));  // open: nQ

  // Notes on the sheet:
  //   1 Bit Register
endmodule

/* Test case Register_test:
Clock	Enable	D_0	Q_0
C	0	0	0
C	0	1	0
C	1	0	0
C	1	1	1
C	1	1	1
C	0	0	1
C	0	1	1
C	1	0	0
*/
