// Digital circuit 4x4_ram.dig as structural Verilog
module _4x4_ram (
  input  D_3,
  input  A_0,
  input  A_1,
  input  C,
  input  D_2,
  input  D_1,
  input  D_0,
  input  en_w,
  input  en_r,
  output O_3,
  output O_2,
  output O_1,
  output O_0
);

  wire and_1_out, decoder_1_out_0, decoder_1_out_1, decoder_1_out_2, decoder_1_out_3, multiplexer_1_out,
       multiplexer_2_out, multiplexer_3_out, multiplexer_4_out, register_1_q, register_2_q, register_3_q,
       register_4_q, register_5_q, register_6_q, register_7_q, register_8_q, register_9_q, register_10_q,
       register_11_q, register_12_q, register_13_q, register_14_q, register_15_q, register_16_q;

  and and_1 (and_1_out, C, en_w);
  Decoder #(.Selector_Bits(2)) decoder_1 (
    .sel({A_1, A_0}), .out_0(decoder_1_out_0), .out_1(decoder_1_out_1), .out_2(decoder_1_out_2),
    .out_3(decoder_1_out_3));
  Register register_1 (.D(D_3), .C(and_1_out), .en(decoder_1_out_0), .Q(register_1_q));
  Register register_2 (.D(D_3), .C(and_1_out), .en(decoder_1_out_1), .Q(register_2_q));
  Register register_3 (.D(D_3), .C(and_1_out), .en(decoder_1_out_2), .Q(register_3_q));
  Register register_4 (.D(D_3), .C(and_1_out), .en(decoder_1_out_3), .Q(register_4_q));
  Multiplexer #(.Selector_Bits(2)) multiplexer_1 (
    .sel({A_1, A_0}), .in_0(register_1_q), .in_1(register_2_q), .in_2(register_3_q), .in_3(register_4_q),
    .out(multiplexer_1_out));
  assign O_3 = en_r ? multiplexer_1_out : 1'bz;  // Driver driver_1
  Register register_5 (.D(D_2), .C(and_1_out), .en(decoder_1_out_0), .Q(register_5_q));
  Register register_6 (.D(D_2), .C(and_1_out), .en(decoder_1_out_1), .Q(register_6_q));
  Register register_7 (.D(D_2), .C(and_1_out), .en(decoder_1_out_2), .Q(register_7_q));
  Register register_8 (.D(D_2), .C(and_1_out), .en(decoder_1_out_3), .Q(register_8_q));
  Multiplexer #(.Selector_Bits(2)) multiplexer_2 (
    .sel({A_1, A_0}), .in_0(register_5_q), .in_1(register_6_q), .in_2(register_7_q), .in_3(register_8_q),
    .out(multiplexer_2_out));
  Register register_9 (.D(D_1), .C(and_1_out), .en(decoder_1_out_0), .Q(register_9_q));
  Register register_10 (.D(D_1), .C(and_1_out), .en(decoder_1_out_1), .Q(register_10_q));
  Register register_11 (.D(D_1), .C(and_1_out), .en(decoder_1_out_2), .Q(register_11_q));
  Register register_12 (.D(D_1), .C(and_1_out), .en(decoder_1_out_3), .Q(register_12_q));
  assign O_2 = en_r ? multiplexer_2_out : 1'bz;  // Driver driver_2
  Multiplexer #(.Selector_Bits(2)) multiplexer_3 (
    .sel({A_1, A_0}), .in_0(register_9_q), .in_1(register_10_q), .in_2(register_11_q), .in_3(register_12_q),
    .out(multiplexer_3_out));
  assign O_1 = en_r ? multiplexer_3_out : 1'bz;  // Driver driver_3
  Register register_13 (.D(D_0), .C(and_1_out), .en(decoder_1_out_0), .Q(register_13_q));
  Register register_14 (.D(D_0), .C(and_1_out), .en(decoder_1_out_1), .Q(register_14_q));
  Register register_15 (.D(D_0), .C(and_1_out), .en(decoder_1_out_2), .Q(register_15_q));
  Register register_16 (.D(D_0), .C(and_1_out), .en(decoder_1_out_3), .Q(register_16_q));
  Multiplexer #(.Selector_Bits(2)) multiplexer_4 (
    .sel({A_1, A_0}), .in_0(register_13_q), .in_1(register_14_q), .in_2(register_15_q), .in_3(register_16_q),
    .out(multiplexer_4_out));
  assign O_0 = en_r ? multiplexer_4_out : 1'bz;  // Driver driver_4

  // Notes on the sheet:
  //   RAM
endmodule

/* Test case RAM_test:
C	en_w	en_r	A_1	A_0	D_0	D_1	D_2	D_3	O_0	O_1	O_2	O_3
C	0	0	X	X	X	X	X	X	Z	Z	Z	Z
C	0	1	X	X	X	X	X	X	0	0	0	0
C	1	0	0	0	1	0	0	0	Z	Z	Z	Z
C	1	0	0	1	0	1	0	0	Z	Z	Z	Z
C	1	0	1	0	0	0	1	0	Z	Z	Z	Z
C	1	0	1	1	0	0	0	1	Z	Z	Z	Z
C	0	1	0	0	X	X	X	X	1	0	0	0
C	0	1	0	1	X	X	X	X	0	1	0	0
C	0	1	1	0	X	X	X	X	0	0	1	0
C	0	1	1	1	X	X	X	X	0	0	0	1
C	1	1	0	0	0	0	0	1	0	0	0	1
*/
