// Digital circuit 8_bit_register.dig as structural Verilog
module _8_bit_register (
  input  Enable,
  input  Clock,
  input  D_0,
  input  D_1,
  input  D_2,
  input  D_3,
  input  D_4,
  input  D_5,
  input  D_6,
  input  D_7,
  output Q_0,
  output Q_1,
  output Q_2,
  output Q_3,
  output Q_4,
  output Q_5,
  output Q_6,
  output Q_7
);

  wire and_1_out, and_2_out, and_3_out, and_4_out, and_5_out, and_6_out, and_7_out, and_8_out, and_9_out,
       and_10_out, and_11_out, and_12_out, and_13_out, and_14_out, and_15_out, and_16_out, not_1_out,
       not_2_out, not_3_out, not_4_out, not_5_out, not_6_out, not_7_out, not_8_out, or_1_out, or_2_out,
       or_3_out, or_4_out, or_5_out, or_6_out, or_7_out, or_8_out;

  not not_1 (not_1_out, Enable);
  not not_2 (not_2_out, Enable);
  not not_3 (not_3_out, Enable);
  not not_4 (not_4_out, Enable);
  not not_5 (not_5_out, Enable);
  not not_6 (not_6_out, Enable);
  not not_7 (not_7_out, Enable);
  not not_8 (not_8_out, Enable);
  and and_1 (and_1_out, Q_0, not_1_out);
  and and_2 (and_2_out, Enable, D_0);
  and and_3 (and_3_out, Q_1, not_2_out);
  and and_4 (and_4_out, Enable, D_1);
  and and_5 (and_5_out, Q_2, not_3_out);
  and and_6 (and_6_out, Enable, D_2);
  and and_7 (and_7_out, Q_3, not_4_out);
  and and_8 (and_8_out, Enable, D_3);
  and and_9 (and_9_out, Q_4, not_5_out);
  and and_10 (and_10_out, Enable, D_4);
  and and_11 (and_11_out, Q_5, not_6_out);
  and and_12 (and_12_out, Enable, D_5);
  and and_13 (and_13_out, Q_6, not_7_out);
  and and_14 (and_14_out, Enable, D_6);
  and and_15 (and_15_out, Q_7, not_8_out);
  and and_16 (and_16_out, Enable, D_7);
  or or_1 (or_1_out, and_1_out, and_2_out);
  or or_2 (or_2_out, and_3_out, and_4_out);
  or or_3 (or_3_out, and_5_out, and_6_out);
  or or_4 (or_4_out, and_7_out, and_8_out);
  or or_5 (or_5_out, and_9_out, and_10_out);
  or or_6 (or_6_out, and_11_out, and_12_out);
  or or_7 (or_7_out, and_13_out, and_14_out);
  or or_8 (or_8_out, and_15_out, and_16_out);
  D_FF d_ff_1 (.D(or_1_out), .C(Clock), .Q(Q_0));  // open: nQ
  D_FF d_ff_2 (.D(or_2_out), .C(Clock), .Q(Q_1));  // open: nQ
  D_FF d_ff_3 (.D(or_3_out), .C(Clock), .Q(Q_2));  // open: nQ
  D_FF d_ff_4 (.D(or_4_out), .C(Clock), .Q(Q_3));  // open: nQ
  D_FF d_ff_5 (.D(or_5_out), .C(Clock), .Q(Q_4));  // open: nQ
  D_FF d_ff_6 (.D(or_6_out), .C(Clock), .Q(Q_5));  // open: nQ
  D_FF d_ff_7 (.D(or_7_out), .C(Clock), .Q(Q_6));  // open: nQ
  D_FF d_ff_8 (.D(or_8_out), .C(Clock), .Q(Q_7));  // open: nQ

  // Notes on the sheet:
  //   8 Bit Register
endmodule

/* Test case Register_test:
Clock	Enable	D_0	Q_0
C	0	0	0
C	0	1	0
C	1	0	0
C	1	1	1
C	1	1	1
C	0	0	1
C	0	1	1
C	1	0	0
*/
