// Digital circuit D_flip_flop.dig as structural Verilog
module D_flip_flop (
  input  D,
  input  C,
  output Q,
  output nQ
);

  wire and_1_out, and_2_out, and_3_out, and_4_out, nor_1_out, nor_2_out, not_1_out, not_2_out, not_3_out;

  not not_1 (not_1_out, C);
  not not_2 (not_2_out, D);
  and and_1 (and_1_out, not_2_out, not_1_out);
  and and_2 (and_2_out, not_1_out, D);
  nor nor_1 (nor_1_out, and_1_out, nor_2_out);
  nor nor_2 (nor_2_out, nor_1_out, and_2_out);
  not not_3 (not_3_out, nor_1_out);
  and and_3 (and_3_out, not_3_out, C);
  and and_4 (and_4_out, C, nor_1_out);
  nor nor_3 (Q, and_3_out, nQ);
  nor nor_4 (nQ, Q, and_4_out);

  // Notes on the sheet:
  //   D Flip-Flop
endmodule

/* Test case D Flip-Flop_test:
C	D	Q	~Q
0	0	X	X
C	0	0	1
0	1	0	1
0	0	0	1
C	1	1	0
0	1	1	0
0	0	1	0
*/
