// Digital circuit D_latch.dig as structural Verilog
module D_latch (
  input  D,
  output Q,
  output nQ
);

  wire not_1_out;

  not not_1 (not_1_out, D);
  nor nor_1 (Q, not_1_out, nQ);
  nor nor_2 (nQ, Q, D);

  // Notes on the sheet:
  //   D Latch
endmodule

/* Test case D Latch_test:
D	Q	~Q
0	X	X
0	0	1
0	0	1
1	1	0
1	1	0
0	0	1
*/
