// Digital circuit D_latch_with_enable.dig as structural Verilog
module D_latch_with_enable (
  input  D,
  input  EN,
  output Q,
  output nQ
);

  wire and_1_out, and_2_out, not_1_out;

  not not_1 (not_1_out, D);
  and and_1 (and_1_out, not_1_out, EN);
  and and_2 (and_2_out, EN, D);
  nor nor_1 (Q, and_1_out, nQ);
  nor nor_2 (nQ, Q, and_2_out);

  // Notes on the sheet:
  //   D Latch with Enable
  //   "R"
  //   "S"
endmodule

/* Test case D Latch with Enable_test:
EN	D	Q	~Q
0	0	X	X
1	0	0	1
0	0	0	1
0	1	0	1
1	1	1	0
0	0	1	0
0	1	1	0
*/
