// Digital circuit SR_latch.dig as structural Verilog
module SR_latch (
  input  R,
  input  S,
  output Q,
  output nQ
);

  nor nor_1 (Q, R, nQ);
  nor nor_2 (nQ, Q, S);

  // Notes on the sheet:
  //   SR Latch
endmodule

/* Test case SR Latch_test:
R	S	Q	~Q
0	0	X	X
0	1	1	0
0	0	1	0
1	0	0	1
0	0	0	1
1	1	0	0
*/
