// Digital circuit SR_latch_with_enable.dig as structural Verilog
module SR_latch_with_enable (
  input  R,
  input  S,
  input  EN,
  output Q,
  output nQ
);

  wire and_1_out, and_2_out;

  and and_1 (and_1_out, R, EN);
  and and_2 (and_2_out, EN, S);
  nor nor_1 (Q, and_1_out, nQ);
  nor nor_2 (nQ, Q, and_2_out);

  // Notes on the sheet:
  //   SR Latch with Enable
endmodule

/* Test case SR Latch with Enable_test:
EN	R	S	Q	~Q
1	0	0	X	X
1	0	1	1	0
1	0	0	1	0
0	0	0	1	0
0	0	1	1	0
0	1	0	1	0
0	1	1	1	0
1	1	0	0	1
1	0	0	0	1
0	0	0	0	1
0	0	1	0	1
0	1	0	0	1
0	1	1	0	1
0	1	0	0	1
1	1	1	0	0
*/
