// Digital circuit address_register_and_RAM.dig as structural Verilog
module address_register_and_RAM (
  input  C,
  input  D_0,
  input  D_1,
  input  D_2,
  input  D_3,
  input  D_4,
  input  D_5,
  input  D_6,
  input  D_7,
  input  address,
  input  RAM_i,
  input  RAM_o,
  output O_0,
  output O_1,
  output O_2,
  output O_3,
  output O_4,
  output O_5,
  output O_6,
  output O_7
);

  wire [3:0] Address_q;

  Register #(.Bits(4)) u_Address (.D({D_3, D_2, D_1, D_0}), .C(C), .en(address), .Q(Address_q));
  RAMSinglePort #(.AddrBits(4), .Bits(8)) ramsingleport_1 (
    .A(Address_q), .str(RAM_i), .C(C), .ld(RAM_o), .D({D_7, D_6, D_5, D_4, D_3, D_2, D_1, D_0}));

  assign O_0 = D_0;
  assign O_1 = D_1;
  assign O_2 = D_2;
  assign O_3 = D_3;
  assign O_4 = D_4;
  assign O_5 = D_5;
  assign O_6 = D_6;
  assign O_7 = D_7;

  // Notes on the sheet:
  //   Address Register and RAM
endmodule

/* Test case Address and RAM_test:
address	RAM_i	RAM_o	D_7	D_6	D_5	D_4	D_3	D_2	D_1	D_0	O_7	O_6	O_5	O_4	O_3	O_2	O_1	O_0	C
# Load patterns in RAM
1	0	0	0	0	0	0	0	0	0	0	0	0	0	0	0	0	0	0	C
0	1	0	1	0	0	0	0	0	0	0	1	0	0	0	0	0	0	0	C
1	0	0	0	0	0	0	0	0	0	1	0	0	0	0	0	0	0	1	C
0	1	0	0	1	0	0	0	0	0	0	0	1	0	0	0	0	0	0	C
1	0	0	0	0	0	0	0	0	1	0	0	0	0	0	0	0	1	0	C
0	1	0	0	0	1	0	0	0	0	0	0	0	1	0	0	0	0	0	C
1	0	0	0	0	0	0	0	0	1	1	0	0	0	0	0	0	1	1	C
0	1	0	0	0	0	1	0	0	0	0	0	0	0	1	0	0	0	0	C
1	0	0	0	0	0	0	0	1	0	0	0	0	0	0	0	1	0	0	C
0	1	0	0	0	0	0	1	0	0	0	0	0	0	0	1	0	0	0	C
1	0	0	0	0	0	0	0	1	0	1	0	0	0	0	0	1	0	1	C
0	1	0	0	0	0	0	0	1	0	0	0	0	0	0	0	1	0	0	C
1	0	0	0	0	0	0	0	1	1	0	0	0	0	0	0	1	1	0	C
0	1	0	0	0	0	0	0	0	1	0	0	0	0	0	0	0	1	0	C
1	0	0	0	0	0	0	0	1	1	1	0	0	0	0	0	1	1	1	C
0	1	0	0	0	0	0	0	0	0	1	0	0	0	0	0	0	0	1	C
# Test output
1	0	0	0	0	0	0	0	0	0	0	0	0	0	0	0	0	0	0	C
0	0	1	Z	Z	Z	Z	Z	Z	Z	Z	1	0	0	0	0	0	0	0	C
1	0	0	0	0	0	0	0	0	0	1	0	0	0	0	0	0	0	1	C
0	0	1	Z	Z	Z	Z	Z	Z	Z	Z	0	1	0	0	0	0	0	0	C
1	0	0	0	0	0	0	0	0	1	0	0	0	0	0	0	0	1	0	C
0	0	1	Z	Z	Z	Z	Z	Z	Z	Z	0	0	1	0	0	0	0	0	C
1	0	0	0	0	0	0	0	0	1	1	0	0	0	0	0	0	1	1	C
0	0	1	Z	Z	Z	Z	Z	Z	Z	Z	0	0	0	1	0	0	0	0	C
1	0	0	0	0	0	0	0	1	0	0	0	0	0	0	0	1	0	0	C
0	0	1	Z	Z	Z	Z	Z	Z	Z	Z	0	0	0	0	1	0	0	0	C
1	0	0	0	0	0	0	0	1	0	1	0	0	0	0	0	1	0	1	C
0	0	1	Z	Z	Z	Z	Z	Z	Z	Z	0	0	0	0	0	1	0	0	C
1	0	0	0	0	0	0	0	1	1	0	0	0	0	0	0	1	1	0	C
0	0	1	Z	Z	Z	Z	Z	Z	Z	Z	0	0	0	0	0	0	1	0	C
1	0	0	0	0	0	0	0	1	1	1	0	0	0	0	0	1	1	1	C
0	0	1	Z	Z	Z	Z	Z	Z	Z	Z	0	0	0	0	0	0	0	1	C
# Ignore top 4 bits
1	0	0	1	1	1	1	0	0	0	0	1	1	1	1	0	0	0	0	C
0	1	0	1	1	1	1	1	1	1	1	1	1	1	1	1	1	1	1	C
1	0	0	0	0	0	0	0	0	0	0	0	0	0	0	0	0	0	0	C
0	0	1	Z	Z	Z	Z	Z	Z	Z	Z	1	1	1	1	1	1	1	1	C
*/
