// Digital circuit subtraction.dig as structural Verilog
module subtraction (
  input  b_0,
  input  b_1,
  input  b_2,
  input  b_3,
  input  b_4,
  input  b_5,
  input  b_6,
  input  b_7,
  input  a_0,
  input  a_1,
  input  a_2,
  input  a_3,
  input  a_4,
  input  a_5,
  input  a_6,
  input  a_7,
  input  sub,
  output o_0,
  output o_1,
  output o_2,
  output o_3,
  output o_4,
  output o_5,
  output o_6,
  output o_7
);

  wire [7:0] xor_1_out;

  assign xor_1_out = {b_7, b_6, b_5, b_4, b_3, b_2, b_1, b_0} ^ {8{sub}};  // XOr xor_1, 8 bits wide
  Add #(.Bits(8)) add_1 (
    .a({a_7, a_6, a_5, a_4, a_3, a_2, a_1, a_0}), .b(xor_1_out), .c_i(sub),
    .s({o_7, o_6, o_5, o_4, o_3, o_2, o_1, o_0}));  // open: c_o

  // Notes on the sheet:
  //   Subtraction
endmodule

/* Test case subtraction_test:
		sub	a_7	a_6	a_5	a_4	a_3	a_2	a_1	a_0	b_7	b_6	b_5	b_4	b_3	b_2	b_1	b_0	o_7	o_6	o_5	o_4	o_3	o_2	o_1	o_0
loop(a, 128)
	loop(b, 128)
		0	bits(8,a)							bits(8,b)							bits(8,a+b)				
		1	bits(8,a)							bits(8,b)							bits(8,a-b)
	end loop
end loop	
*/
