// Digital circuit twos_complement_negation.dig as structural Verilog
module twos_complement_negation (
  input  i_0,
  input  i_1,
  input  i_2,
  input  i_3,
  input  i_4,
  input  i_5,
  input  i_6,
  input  i_7,
  output o_0,
  output o_1,
  output o_2,
  output o_3,
  output o_4,
  output o_5,
  output o_6,
  output o_7
);

  wire pullup_1_out;
  wire [7:0] not_1_out;
  wire [7:7] pulldown_1_out;

  PullDown pulldown_1 (.out(pulldown_1_out[7]));
  assign not_1_out = ~{i_7, i_6, i_5, i_4, i_3, i_2, i_1, i_0};  // Not not_1, 8 bits wide
  PullUp pullup_1 (.out(pullup_1_out));
  Add #(.Bits(8)) add_1 (
    .a(not_1_out), .b({8{pulldown_1_out[7]}}), .c_i(pullup_1_out),
    .s({o_7, o_6, o_5, o_4, o_3, o_2, o_1, o_0}));  // open: c_o

  // Notes on the sheet:
  //   Two's Complement Negation
endmodule

/* Test case negation_test:
	i_7	i_6	i_5	i_4	i_3	i_2	i_1	i_0	o_7	o_6	o_5	o_4	o_3	o_2	o_1	o_0
loop(a, 128)
	bits(8,a)							bits(8,-a)
end loop
*/
