// Digital circuit output_register_and_seven_segment_display.dig as structural Verilog
module output_register_and_seven_segment_display (
  input  PC_o,
  input  PC_i,
  input  D_0,
  input  D_1,
  input  D_2,
  input  D_3,
  input  C,
  input  PC_e,
  input  D_4,
  input  D_5,
  input  D_6,
  input  D_7,
  input  D_8,
  input  D_9,
  input  D_10,
  input  D_11,
  input  D_12,
  input  D_13,
  input  D_14,
  input  D_15,
  input  \signed ,
  output O_0,
  output O_1,
  output O_2,
  output O_3,
  output O_4,
  output O_5,
  output O_6,
  output O_7
);

  wire or_1_out;
  wire [3:0] add_1_s, lookuptable_1_out, lookuptable_1_out_2, lookuptable_1_out_3, lookuptable_1_out_4,
       lookuptable_1_out_5, lookuptable_1_out_6, multiplexer_1_out, register_1_q;
  wire [24:24] lookuptable_1_out_7;

  LookUpTable #(.Bits(25)) lookuptable_1 (
    .in0(D_8), .in1(D_9), .in2(D_10), .in3(D_11), .in4(D_12), .in5(D_13), .in6(D_14), .in7(D_15),
    .in8(\signed ),
    .out({lookuptable_1_out_7[24], lookuptable_1_out_6, lookuptable_1_out_5, lookuptable_1_out_4, lookuptable_1_out_3, lookuptable_1_out_2, lookuptable_1_out}));
  // Probe - on lookuptable_1_out_7[24]
  // Probe 10s on {lookuptable_1_out_4, lookuptable_1_out_3}
  // Probe 100s on {lookuptable_1_out_6, lookuptable_1_out_5}
  Seven_Seg seven_seg_1 (
    .a(1'b0), .b(1'b0), .c(1'b0), .d(1'b0), .e(1'b0), .f(1'b0), .g(lookuptable_1_out_7[24]), .dp(1'b0));
  // Probe 1s on {lookuptable_1_out_2, lookuptable_1_out}
  Seven_Seg seven_seg_2 (
    .a(lookuptable_1_out_5[0]), .b(lookuptable_1_out_5[1]), .c(lookuptable_1_out_5[2]),
    .d(lookuptable_1_out_5[3]), .e(lookuptable_1_out_6[0]), .f(lookuptable_1_out_6[1]),
    .g(lookuptable_1_out_6[2]), .dp(lookuptable_1_out_6[3]));
  Seven_Seg seven_seg_3 (
    .a(lookuptable_1_out_3[0]), .b(lookuptable_1_out_3[1]), .c(lookuptable_1_out_3[2]),
    .d(lookuptable_1_out_3[3]), .e(lookuptable_1_out_4[0]), .f(lookuptable_1_out_4[1]),
    .g(lookuptable_1_out_4[2]), .dp(lookuptable_1_out_4[3]));
  Seven_Seg seven_seg_4 (
    .a(lookuptable_1_out[0]), .b(lookuptable_1_out[1]), .c(lookuptable_1_out[2]), .d(lookuptable_1_out[3]),
    .e(lookuptable_1_out_2[0]), .f(lookuptable_1_out_2[1]), .g(lookuptable_1_out_2[2]),
    .dp(lookuptable_1_out_2[3]));
  Multiplexer #(.Bits(4)) multiplexer_1 (
    .sel(PC_i), .in_0(add_1_s), .in_1({D_3, D_2, D_1, D_0}), .out(multiplexer_1_out));
  or or_1 (or_1_out, PC_e, PC_i);
  Register #(.Bits(4)) register_1 (.D(multiplexer_1_out), .C(C), .en(or_1_out), .Q(register_1_q));
  Add #(.Bits(4)) add_1 (.a(register_1_q), .b(4'b0001), .c_i(1'b0), .s(add_1_s));  // open: c_o
  assign {D_7, D_6, D_5, D_4, D_3, D_2, D_1, D_0} = PC_o ? {4'b0000, register_1_q} : 8'bz;  // Driver driver_1

  assign O_0 = D_0;
  assign O_1 = D_1;
  assign O_2 = D_2;
  assign O_3 = D_3;
  assign O_4 = D_4;
  assign O_5 = D_5;
  assign O_6 = D_6;
  assign O_7 = D_7;

  // Notes on the sheet:
  //   Output Display
  //   contents of lookuptable_1 (hex, n*v repeats v):
  //   3f3f3f,3f3f06,3f3f5b,3f3f4f,3f3f66,3f3f6d,3f3f7d,3f3f07,3f3f7f
  //   ,3f3f6f,3f063f,3f0606,3f065b,3f064f,3f0666,3f066d,3f067d,3f0607
  //   ,3f067f,3f066f,3f5b3f,3f5b06,3f5b5b,3f5b4f,3f5b66,3f5b6d,3f5b7d
  //   ,3f5b07,3f5b7f,3f5b6f,3f4f3f,3f4f06,3f4f5b,3f4f4f,3f4f66,3f4f6d
  //   ,3f4f7d,3f4f07,3f4f7f,3f4f6f,3f663f,3f6606,3f665b,3f664f,3f6666
  //   ,3f666d,3f667d,3f6607,3f667f,3f666f,3f6d3f,3f6d06,3f6d5b,3f6d4f
  //   ,3f6d66,3f6d6d,3f6d7d,3f6d07,3f6d7f,3f6d6f,3f7d3f,3f7d06,3f7d5b
  //   ,3f7d4f,3f7d66,3f7d6d,3f7d7d,3f7d07,3f7d7f,3f7d6f,3f073f,3f0706
  //   ,3f075b,3f074f,3f0766,3f076d,3f077d,3f0707,3f077f,3f076f,3f7f3f
  //   ,3f7f06,3f7f5b,3f7f4f,3f7f66,3f7f6d,3f7f7d,3f7f07,3f7f7f,3f7f6f
  //   ,3f6f3f,3f6f06,3f6f5b,3f6f4f,3f6f66,3f6f6d,3f6f7d,3f6f07,3f6f7f
  //   ,3f6f6f,63f3f,63f06,63f5b,63f4f,63f66,63f6d,63f7d,63f07,63f7f
  //   ,63f6f,6063f,60606,6065b,6064f,60666,6066d,6067d,60607,6067f,6066f
  //   ,65b3f,65b06,65b5b,65b4f,65b66,65b6d,65b7d,65b07,65b7f,65b6f,64f3f
  //   ,64f06,64f5b,64f4f,64f66,64f6d,64f7d,64f07,64f7f,64f6f,6663f,66606
  //   ,6665b,6664f,66666,6666d,6667d,66607,6667f,6666f,66d3f,66d06,66d5b
  //   ,66d4f,66d66,66d6d,66d7d,66d07,66d7f,66d6f,67d3f,67d06,67d5b,67d4f
  //   ,67d66,67d6d,67d7d,67d07,67d7f,67d6f,6073f,60706,6075b,6074f,60766
  //   ,6076d,6077d,60707,6077f,6076f,67f3f,67f06,67f5b,67f4f,67f66,67f6d
  //   ,67f7d,67f07,67f7f,67f6f,66f3f,66f06,66f5b,66f4f,66f66,66f6d,66f7d
  //   ,66f07,66f7f,66f6f,5b3f3f,5b3f06,5b3f5b,5b3f4f,5b3f66,5b3f6d,5b3f7d
  //   ,5b3f07,5b3f7f,5b3f6f,5b063f,5b0606,5b065b,5b064f,5b0666,5b066d
  //   ,5b067d,5b0607,5b067f,5b066f,5b5b3f,5b5b06,5b5b5b,5b5b4f,5b5b66
  //   ,5b5b6d,5b5b7d,5b5b07,5b5b7f,5b5b6f,5b4f3f,5b4f06,5b4f5b,5b4f4f
  //   ,5b4f66,5b4f6d,5b4f7d,5b4f07,5b4f7f,5b4f6f,5b663f,5b6606,5b665b
  //   ,5b664f,5b6666,5b666d,5b667d,5b6607,5b667f,5b666f,5b6d3f,5b6d06
  //   ,5b6d5b,5b6d4f,5b6d66,5b6d6d,3f3f3f,3f3f06,3f3f5b,3f3f4f,3f3f66
  //   ,3f3f6d,3f3f7d,3f3f07,3f3f7f,3f3f6f,3f063f,3f0606,3f065b,3f064f
  //   ,3f0666,3f066d,3f067d,3f0607,3f067f,3f066f,3f5b3f,3f5b06,3f5b5b
  //   ,3f5b4f,3f5b66,3f5b6d,3f5b7d,3f5b07,3f5b7f,3f5b6f,3f4f3f,3f4f06
  //   ,3f4f5b,3f4f4f,3f4f66,3f4f6d,3f4f7d,3f4f07,3f4f7f,3f4f6f,3f663f
  //   ,3f6606,3f665b,3f664f,3f6666,3f666d,3f667d,3f6607,3f667f,3f666f
  //   ,3f6d3f,3f6d06,3f6d5b,3f6d4f,3f6d66,3f6d6d,3f6d7d,3f6d07,3f6d7f
  //   ,3f6d6f,3f7d3f,3f7d06,3f7d5b,3f7d4f,3f7d66,3f7d6d,3f7d7d,3f7d07
  //   ,3f7d7f,3f7d6f,3f073f,3f0706,3f075b,3f074f,3f0766,3f076d,3f077d
  //   ,3f0707,3f077f,3f076f,3f7f3f,3f7f06,3f7f5b,3f7f4f,3f7f66,3f7f6d
  //   ,3f7f7d,3f7f07,3f7f7f,3f7f6f,3f6f3f,3f6f06,3f6f5b,3f6f4f,3f6f66
  //   ,3f6f6d,3f6f7d,3f6f07,3f6f7f,3f6f6f,63f3f,63f06,63f5b,63f4f,63f66
  //   ,63f6d,63f7d,63f07,63f7f,63f6f,6063f,60606,6065b,6064f,60666,6066d
  //   ,6067d,60607,6067f,6066f,65b3f,65b06,65b5b,65b4f,65b66,65b6d,65b7d
  //   ,65b07,1065b7f,1065b07,1065b7d,1065b6d,1065b66,1065b4f,1065b5b
  //   ,1065b06,1065b3f,106066f,106067f,1060607,106067d,106066d,1060666
  //   ,106064f,106065b,1060606,106063f,1063f6f,1063f7f,1063f07,1063f7d
  //   ,1063f6d,1063f66,1063f4f,1063f5b,1063f06,1063f3f,13f6f6f,13f6f7f
  //   ,13f6f07,13f6f7d,13f6f6d,13f6f66,13f6f4f,13f6f5b,13f6f06,13f6f3f
  //   ,13f7f6f,13f7f7f,13f7f07,13f7f7d,13f7f6d,13f7f66,13f7f4f,13f7f5b
  //   ,13f7f06,13f7f3f,13f076f,13f077f,13f0707,13f077d,13f076d,13f0766
  //   ,13f074f,13f075b,13f0706,13f073f,13f7d6f,13f7d7f,13f7d07,13f7d7d
  //   ,13f7d6d,13f7d66,13f7d4f,13f7d5b,13f7d06,13f7d3f,13f6d6f,13f6d7f
  //   ,13f6d07,13f6d7d,13f6d6d,13f6d66,13f6d4f,13f6d5b,13f6d06,13f6d3f
  //   ,13f666f,13f667f,13f6607,13f667d,13f666d,13f6666,13f664f,13f665b
  //   ,13f6606,13f663f,13f4f6f,13f4f7f,13f4f07,13f4f7d,13f4f6d,13f4f66
  //   ,13f4f4f,13f4f5b,13f4f06,13f4f3f,13f5b6f,13f5b7f,13f5b07,13f5b7d
  //   ,13f5b6d,13f5b66,13f5b4f,13f5b5b,13f5b06,13f5b3f,13f066f,13f067f
  //   ,13f0607,13f067d,13f066d,13f0666,13f064f,13f065b,13f0606,13f063f
  //   ,13f3f6f,13f3f7f,13f3f07,13f3f7d,13f3f6d,13f3f66,13f3f4f,13f3f5b,13f3f06
  //   Program Counter
endmodule

/* Test case output_test:
signed	D_7	D_6	D_5	D_4	D_3	D_2	D_1	D_0	-	100s	10s	1s
# Test unsigned 00 -- 10 
0	0	0	0	0	0	0	0	0	0	0x3F	0x3F	0x3F
0	0	0	0	0	0	0	0	1	0	0x3F	0x3F	0x06
0	0	0	0	0	0	0	1	0	0	0x3F	0x3F	0x5B
0	0	0	0	0	0	0	1	1	0	0x3F	0x3F	0x4F
0	0	0	0	0	0	1	0	0	0	0x3F	0x3F	0x66
0	0	0	0	0	0	1	0	1	0	0x3F	0x3F	0x6D
0	0	0	0	0	0	1	1	0	0	0x3F	0x3F	0x7D
0	0	0	0	0	0	1	1	1	0	0x3F	0x3F	0x07
0	0	0	0	0	1	0	0	0	0	0x3F	0x3F	0x7F
0	0	0	0	0	1	0	0	1	0	0x3F	0x3F	0x6F
0	0	0	0	0	1	0	1	0	0	0x3F	0x06	0x3F
# Test unsigned 11 -- 99, by 11s (11 -> 22 -> 33...)
0	0	0	0	0	1	0	1	1	0	0x3F	0x06	0x06
0	0	0	0	1	0	1	1	0	0	0x3F	0x5B	0x5B
0	0	0	1	0	0	0	0	1	0	0x3F	0x4F	0x4F
0	0	0	1	0	1	1	0	0	0	0x3F	0x66	0x66
0	0	0	1	1	0	1	1	1	0	0x3F	0x6D	0x6D
0	0	1	0	0	0	0	1	0	0	0x3F	0x7D	0x7D
0	0	1	0	0	1	1	0	1	0	0x3F	0x07	0x07
0	0	1	0	1	1	0	0	0	0	0x3F	0x7F	0x7F
0	0	1	1	0	0	0	1	1	0	0x3F	0x6F	0x6F
# Test unsigned 111, 222, and 255
0	0	1	1	0	1	1	1	1	0	0x06	0x06	0x06
0	1	1	0	1	1	1	1	0	0	0x5B	0x5B	0x5B
0	1	1	1	1	1	1	1	1	0	0x5B	0x6D	0x6D
# Test signed 0, 1, 127 and -128, -127, and -2, -1
1	0	0	0	0	0	0	0	0	0	0x3F	0x3F	0x3F
1	0	0	0	0	0	0	0	1	0	0x3F	0x3F	0x06
1	0	1	1	1	1	1	1	1	0	0x06	0x5B	0x07
1	1	0	0	0	0	0	0	0	1	0x06	0x5B	0x7F
1	1	0	0	0	0	0	0	1	1	0x06	0x5B	0x07
1	1	1	1	1	1	1	1	0	1	0x3F	0x3F	0x5B
1	1	1	1	1	1	1	1	1	1	0x3F	0x3F	0x06
*/

/* Test case PC_test:
	PC_e	PC_i	PC_o	D_7	D_6	D_5	D_4	D_3	D_2	D_1	D_0	O_7	O_6	O_5	O_4	O_3	O_2	O_1	O_0	C
	0	0	0	0	0	0	0	0	0	0	0	0	0	0	0	0	0	0	0	C
# Pulse with No Enable Causes No Change 
	0	0	1	Z	Z	Z	Z	Z	Z	Z	Z	0	0	0	0	0	0	0	0	C
# Pulse with Enable and No Output Still counts
	1	0	0	z	Z	Z	Z	Z	Z	Z	Z	Z	Z	Z	Z	Z	Z	Z	Z	C
	1	0	0	Z	Z	Z	Z	Z	Z	Z	z	Z	Z	Z	Z	Z	Z	Z	Z	C
	0	0	1	Z	Z	Z	Z	Z	Z	Z	Z	0	0	0	0	0	0	1	0	C
# Load 0 into program counter and confirm
	X	1	0	0	0	0	0	0	0	0	0	0	0	0	0	0	0	0	0	C
	0	0	1	Z	Z	Z	Z	Z	Z	Z	Z	0	0	0	0	0	0	0	0	C
# Pulse clock 15 times to count to 1 -> 2 -> ... -> 15 -> 0
loop(i, 15)
	1	0	1	Z	Z	Z	Z	Z	Z	Z	Z	0	0	0	0	bits(4, i+1)			C
end loop
# Ignore top 4 bits
	0	1	0	0	1	0	1	0	1	0	1	0	1	0	1	0	1	0	1	c
	0	0	1	z	z	z	z	z	z	z	z	0	0	0	0	0	1	0	1	c
*/
