// Digital circuit program_counter.dig as structural Verilog
module program_counter (
  input  PC_o,
  input  PC_i,
  input  D_0,
  input  D_1,
  input  D_2,
  input  D_3,
  input  C,
  input  PC_e,
  input  D_4,
  input  D_5,
  input  D_6,
  input  D_7,
  output O_0,
  output O_1,
  output O_2,
  output O_3,
  output O_4,
  output O_5,
  output O_6,
  output O_7
);

  wire or_1_out;
  wire [3:0] add_1_s, multiplexer_1_out, register_1_q;

  Multiplexer #(.Bits(4)) multiplexer_1 (
    .sel(PC_i), .in_0(add_1_s), .in_1({D_3, D_2, D_1, D_0}), .out(multiplexer_1_out));
  or or_1 (or_1_out, PC_i, PC_e);
  Register #(.Bits(4)) register_1 (.D(multiplexer_1_out), .C(C), .en(or_1_out), .Q(register_1_q));
  Add #(.Bits(4)) add_1 (.a(register_1_q), .b(4'b0001), .c_i(1'b0), .s(add_1_s));  // open: c_o
  assign {D_7, D_6, D_5, D_4, D_3, D_2, D_1, D_0} = PC_o ? {4'b0000, register_1_q} : 8'bz;  // Driver driver_1

  assign O_0 = D_0;
  assign O_1 = D_1;
  assign O_2 = D_2;
  assign O_3 = D_3;
  assign O_4 = D_4;
  assign O_5 = D_5;
  assign O_6 = D_6;
  assign O_7 = D_7;

  // Notes on the sheet:
  //   Program Counter
endmodule

/* Test case PC_test:
	PC_e	PC_i	PC_o	D_7	D_6	D_5	D_4	D_3	D_2	D_1	D_0	O_7	O_6	O_5	O_4	O_3	O_2	O_1	O_0	C
	0	0	0	0	0	0	0	0	0	0	0	0	0	0	0	0	0	0	0	C
# Pulse with No Enable Causes No Change 
	0	0	1	Z	Z	Z	Z	Z	Z	Z	Z	0	0	0	0	0	0	0	0	C
# Pulse with Enable and No Output Still counts
	1	0	0	z	Z	Z	Z	Z	Z	Z	Z	Z	Z	Z	Z	Z	Z	Z	Z	C
	1	0	0	Z	Z	Z	Z	Z	Z	Z	z	Z	Z	Z	Z	Z	Z	Z	Z	C
	0	0	1	Z	Z	Z	Z	Z	Z	Z	Z	0	0	0	0	0	0	1	0	C
# Load 0 into program counter and confirm
	X	1	0	0	0	0	0	0	0	0	0	0	0	0	0	0	0	0	0	C
	0	0	1	Z	Z	Z	Z	Z	Z	Z	Z	0	0	0	0	0	0	0	0	C
# Pulse clock 15 times to count to 1 -> 2 -> ... -> 15 -> 0
loop(i, 15)
	1	0	1	Z	Z	Z	Z	Z	Z	Z	Z	0	0	0	0	bits(4, i+1)			C
end loop
# Ignore top 4 bits
	0	1	0	0	1	0	1	0	1	0	1	0	1	0	1	0	1	0	1	c
	0	0	1	z	z	z	z	z	z	z	z	0	0	0	0	0	1	0	1	c
*/
