// Digital circuit boolean_operators_with_transistors.dig as structural Verilog
module boolean_operators_with_transistors (
  input  NOT_a,
  input  OR_a,
  input  OR_b,
  input  AND_a,
  input  AND_b,
  output NOT_o,
  output OR_o,
  output AND_o
);

  wire nfet_4_s;

  PullUp pullup_1 (.out(NOT_o));
  NFET nfet_1 (.G(NOT_a), .D(NOT_o), .S(1'b0));
  NFET nfet_2 (.G(OR_a), .D(1'b1), .S(OR_o));
  NFET nfet_3 (.G(OR_b), .D(1'b1), .S(OR_o));
  PullDown pulldown_1 (.out(OR_o));
  NFET nfet_4 (.G(AND_a), .D(1'b1), .S(nfet_4_s));
  NFET nfet_5 (.G(AND_b), .D(nfet_4_s), .S(AND_o));
  PullDown pulldown_2 (.out(AND_o));

  // Notes on the sheet:
  //   NOT
  //   OR
  //   AND
endmodule

/* Test case NOT_test:
NOT_a 	NOT_o
0	1
1	0
*/

/* Test case OR_test:
OR_a	OR_b	OR_o
0	0	0
0	1	1
1	0	1
1	1	1
*/

/* Test case AND_test:
AND_a	AND_b	AND_o
0	0	0
0	1	0
1	0	0
1	1	1
*/
