// Digital circuit transistor_as_switch.dig as structural Verilog
module transistor_as_switch (
  input  switch_a,
  output switch_o
);

  NFET nfet_1 (.G(switch_a), .D(1'b1), .S(switch_o));
  PullDown pulldown_1 (.out(switch_o));

  // Notes on the sheet:
  //   Transistor as Switch
endmodule

/* Test case switch_tests:
switch_a	switch_o
0		0
1		1
*/
